// Logisim project 7segs.circ as structural Verilog: 2 circuits, main circuit main
module main (
);

  wire and_1_out, and_2_out, and_3_out, and_4_out, buffer_1_out, button_1_out, button_2_out, display_1_a_2,
       display_1_b_2, display_1_c_2, display_1_d_2, display_1_e, display_1_f, display_1_g, display_2_a_2,
       display_2_b_2, display_2_c_2, display_2_d_2, display_2_e, display_2_f, display_2_g, not_1_out,
       not_2_out, not_3_out, t_ff_1_q, t_ff_1_qn, t_ff_2_q, t_ff_3_q, t_ff_3_qn, t_ff_4_q, t_ff_4_qn,
       t_ff_5_q, t_ff_5_qn, t_ff_6_q, t_ff_7_q, t_ff_7_qn, t_ff_8_q, t_ff_8_qn, xor_1_out;

  Button button_1 (.out(button_1_out));
  Button button_2 (.out(button_2_out));
  not not_1 (not_1_out, t_ff_3_qn);
  not not_2 (not_2_out, t_ff_4_qn);
  not not_3 (not_3_out, t_ff_5_qn);
  T_Flip_Flop t_ff_1 (.clk(t_ff_7_qn), .T(1'b1), .Q(t_ff_1_q), .Qn(t_ff_1_qn), .reset(and_2_out));  // open: preset, en
  T_Flip_Flop t_ff_2 (.clk(not_1_out), .T(1'b1), .Q(t_ff_2_q), .preset(xor_1_out));  // open: Qn, reset, en
  T_Flip_Flop t_ff_3 (.clk(not_2_out), .T(1'b1), .Q(t_ff_3_q), .Qn(t_ff_3_qn), .reset(xor_1_out));  // open: preset, en
  T_Flip_Flop t_ff_4 (.clk(not_3_out), .T(1'b1), .Q(t_ff_4_q), .Qn(t_ff_4_qn), .reset(xor_1_out));  // open: preset, en
  T_Flip_Flop t_ff_5 (
    .clk(button_1_out), .T(1'b1), .Q(t_ff_5_q), .Qn(t_ff_5_qn), .preset(xor_1_out));  // open: reset, en
  xor xor_1 (xor_1_out, and_1_out, and_4_out);
  T_Flip_Flop t_ff_6 (.clk(t_ff_1_qn), .T(1'b1), .Q(t_ff_6_q), .reset(and_2_out));  // open: Qn, preset, en
  T_Flip_Flop t_ff_7 (.clk(t_ff_8_qn), .T(1'b1), .Q(t_ff_7_q), .Qn(t_ff_7_qn), .reset(and_2_out));  // open: preset, en
  T_Flip_Flop t_ff_8 (
    .clk(button_2_out), .T(1'b1), .Q(t_ff_8_q), .Qn(t_ff_8_qn), .reset(and_2_out));  // open: preset, en
  buf buffer_1 (buffer_1_out, and_3_out);
  and and_1 (and_1_out, buffer_1_out, t_ff_2_q);
  and and_2 (and_2_out, t_ff_6_q, t_ff_7_q);
  and and_3 (and_3_out, t_ff_4_q, t_ff_3_q, t_ff_5_q);
  and and_4 (and_4_out, t_ff_2_q, t_ff_5_q, t_ff_3_q, t_ff_4_q);
  Display display_1 (
    .A(t_ff_2_q), .B(t_ff_3_q), .C(t_ff_4_q), .D(t_ff_5_q), .a_2(display_1_a_2), .b_2(display_1_b_2),
    .c_2(display_1_c_2), .d_2(display_1_d_2), .e(display_1_e), .f(display_1_f), .g(display_1_g));
  Display display_2 (
    .A(t_ff_6_q), .B(t_ff_1_q), .C(t_ff_7_q), .D(t_ff_8_q), .a_2(display_2_a_2), .b_2(display_2_b_2),
    .c_2(display_2_c_2), .d_2(display_2_d_2), .e(display_2_e), .f(display_2_f), .g(display_2_g));
  _7_Segment_Display u_7_segment_display_1 (
    .g(display_2_g), .f(display_2_f), .a(display_2_a_2), .b(display_2_b_2), .e(display_2_e),
    .d(display_2_d_2), .c(display_2_c_2));  // open: dp
  _7_Segment_Display u_7_segment_display_2 (
    .g(display_1_g), .f(display_1_f), .a(display_1_a_2), .b(display_1_b_2), .e(display_1_e),
    .d(display_1_d_2), .c(display_1_c_2));  // open: dp
endmodule

module Display (
  input  A,
  input  B,
  input  C,
  input  D,
  output a_2,
  output b_2,
  output c_2,
  output d_2,
  output e,
  output f,
  output g
);

  wire and_1_out, and_2_out, and_3_out, and_4_out, and_5_out, and_6_out, and_7_out, and_8_out, and_9_out,
       and_10_out, and_11_out, and_12_out, and_13_out, and_14_out, and_15_out, and_16_out, and_17_out,
       and_18_out, and_19_out, and_20_out, and_21_out, and_22_out, and_23_out, and_24_out, and_25_out,
       not_1_out, not_2_out, not_3_out, not_4_out, not_5_out, not_6_out, not_7_out, not_8_out, not_9_out,
       not_10_out, not_11_out, not_12_out, not_13_out, not_14_out, not_15_out, not_16_out, not_17_out,
       not_18_out, not_19_out, not_20_out, not_21_out, not_22_out, not_23_out, not_24_out, not_25_out,
       not_26_out, not_27_out, not_28_out, not_29_out, not_30_out, not_31_out, not_32_out, not_33_out,
       not_34_out, not_35_out, not_36_out, not_37_out, not_38_out, not_39_out, not_40_out, not_41_out,
       not_42_out, not_43_out, not_44_out, not_45_out, not_46_out, not_47_out;

  not not_1 (not_1_out, A);
  and and_1 (and_1_out, not_1_out, not_2_out, not_3_out);
  not not_2 (not_2_out, B);
  not not_3 (not_3_out, D);
  not not_4 (not_4_out, A);
  and and_2 (and_2_out, not_4_out, C);
  not not_5 (not_5_out, A);
  and and_3 (and_3_out, not_5_out, B, D);
  and and_4 (and_4_out, A, not_6_out, not_7_out);
  not not_6 (not_6_out, B);
  not not_7 (not_7_out, C);
  not not_8 (not_8_out, A);
  and and_5 (and_5_out, not_8_out, not_9_out);
  not not_9 (not_9_out, B);
  not not_10 (not_10_out, A);
  and and_6 (and_6_out, not_10_out, not_11_out, not_12_out);
  not not_11 (not_11_out, C);
  not not_12 (not_12_out, D);
  not not_13 (not_13_out, B);
  and and_7 (and_7_out, not_13_out, not_14_out);
  not not_14 (not_14_out, C);
  not not_15 (not_15_out, A);
  and and_8 (and_8_out, not_15_out, C, D);
  not not_16 (not_16_out, B);
  and and_9 (and_9_out, not_16_out, not_17_out);
  not not_17 (not_17_out, C);
  not not_18 (not_18_out, A);
  and and_10 (and_10_out, not_18_out, D);
  not not_19 (not_19_out, A);
  and and_11 (and_11_out, not_19_out, B);
  not not_20 (not_20_out, A);
  not not_21 (not_21_out, B);
  not not_22 (not_22_out, D);
  not not_23 (not_23_out, A);
  not not_24 (not_24_out, B);
  not not_25 (not_25_out, A);
  not not_26 (not_26_out, D);
  not not_27 (not_27_out, A);
  not not_28 (not_28_out, C);
  not not_29 (not_29_out, B);
  not not_30 (not_30_out, C);
  not not_31 (not_31_out, B);
  and and_12 (and_12_out, not_31_out, not_32_out, not_33_out);
  not not_32 (not_32_out, C);
  not not_33 (not_33_out, D);
  not not_34 (not_34_out, A);
  and and_13 (and_13_out, not_34_out, C, not_35_out);
  not not_35 (not_35_out, D);
  not not_36 (not_36_out, A);
  and and_14 (and_14_out, not_36_out, not_37_out, not_38_out);
  not not_37 (not_37_out, C);
  not not_38 (not_38_out, D);
  not not_39 (not_39_out, A);
  and and_15 (and_15_out, not_39_out, B, not_40_out);
  not not_40 (not_40_out, C);
  not not_41 (not_41_out, A);
  and and_16 (and_16_out, not_41_out, B, not_42_out);
  not not_42 (not_42_out, D);
  and and_17 (and_17_out, A, not_43_out, not_44_out);
  not not_43 (not_43_out, B);
  not not_44 (not_44_out, C);
  not not_45 (not_45_out, B);
  and and_18 (and_18_out, not_45_out, C);
  and and_19 (and_19_out, B, not_46_out);
  not not_46 (not_46_out, C);
  and and_20 (and_20_out, B, not_47_out);
  not not_47 (not_47_out, D);
  or or_1 (a_2, and_1_out, and_2_out, and_3_out, and_4_out);
  or or_2 (b_2, and_5_out, and_6_out, and_7_out, and_8_out);
  or or_3 (c_2, and_9_out, and_10_out, and_11_out);
  and and_21 (and_21_out, not_20_out, not_21_out, not_22_out);
  and and_22 (and_22_out, not_23_out, not_24_out, C);
  and and_23 (and_23_out, not_25_out, C, not_26_out);
  and and_24 (and_24_out, not_27_out, B, not_28_out, D);
  and and_25 (and_25_out, A, not_29_out, not_30_out);
  or or_4 (e, and_12_out, and_13_out);
  or or_5 (f, and_14_out, and_15_out, and_16_out, and_17_out);
  or or_6 (g, and_18_out, and_19_out, and_20_out, A);
  or or_7 (d_2, and_21_out, and_22_out, and_23_out, and_24_out, and_25_out);
endmodule
