// Logisim project AdderSubIncDec.circ as structural Verilog: 3 circuits, main circuit main
module main (
  input  [3:0] in_1,
  input  [3:0] in_2,
  input  [1:0] in_3,
  output [4:0] out_4
);

  wire [4:0] adder_1_c0, adder_2_c0, subtractor_1_c0, subtractor_2_c0;

  Adder adder_1 (
    .B3(in_2[3]), .A3(in_1[3]), .B2(in_2[2]), .A2(in_1[2]), .B1(in_2[1]), .A1(in_1[1]), .B0(in_2[0]),
    .A0(in_1[0]), .CarryOut(adder_1_c0[4]), .C3(adder_1_c0[3]), .C2(adder_1_c0[2]), .C1(adder_1_c0[1]),
    .C0(adder_1_c0[0]));
  Subtractor subtractor_1 (
    .B3(in_2[3]), .A3(in_1[3]), .B2(in_2[2]), .A2(in_1[2]), .B1(in_2[1]), .A1(in_1[1]), .B0(in_2[0]),
    .A0(in_1[0]), .C3(subtractor_1_c0[3]), .C2(subtractor_1_c0[2]), .C1(subtractor_1_c0[1]),
    .C0(subtractor_1_c0[0]));  // open: Borrow
  Adder adder_2 (
    .B3(1'b0), .A3(in_1[3]), .B2(1'b0), .A2(in_1[2]), .B1(1'b0), .A1(in_1[1]), .B0(1'b1), .A0(in_1[0]),
    .CarryOut(adder_2_c0[4]), .C3(adder_2_c0[3]), .C2(adder_2_c0[2]), .C1(adder_2_c0[1]), .C0(adder_2_c0[0]));
  Subtractor subtractor_2 (
    .B3(1'b0), .A3(in_1[3]), .B2(1'b0), .A2(in_1[2]), .B1(1'b0), .A1(in_1[1]), .B0(1'b1), .A0(in_1[0]),
    .Borrow(subtractor_2_c0[4]), .C3(subtractor_2_c0[3]), .C2(subtractor_2_c0[2]), .C1(subtractor_2_c0[1]),
    .C0(subtractor_2_c0[0]));
  Multiplexer #(.select(2), .width(5)) multiplexer_1 (
    .in0(adder_1_c0), .in1(subtractor_1_c0), .in2(adder_2_c0), .in3(subtractor_2_c0), .out(out_4), .sel(in_3));  // open: en
endmodule

module Adder (
  input  B3,
  input  A3,
  input  B2,
  input  A2,
  input  B1,
  input  A1,
  input  B0,
  input  A0,
  output CarryOut,
  output C3,
  output C2,
  output C1,
  output C0
);

  wire adder_2_cout, adder_3_cout, adder_4_cout;

  Adder_part #(.width(1)) adder_1 (.a(A3), .b(B3), .out(C3), .cin(adder_2_cout), .cout(CarryOut));
  Adder_part #(.width(1)) adder_2 (.a(A2), .b(B2), .out(C2), .cin(adder_3_cout), .cout(adder_2_cout));
  Adder_part #(.width(1)) adder_3 (.a(A1), .b(B1), .out(C1), .cin(adder_4_cout), .cout(adder_3_cout));
  Adder_part #(.width(1)) adder_4 (.a(A0), .b(B0), .out(C0), .cout(adder_4_cout));  // open: cin
endmodule

module Subtractor (
  input  B3,
  input  A3,
  input  B2,
  input  A2,
  input  B1,
  input  A1,
  input  B0,
  input  A0,
  output Borrow,
  output C3,
  output C2,
  output C1,
  output C0
);

  wire adder_2_cout, adder_3_cout, adder_4_cout, not_1_out, not_2_out, not_3_out, not_4_out;

  not not_1 (not_1_out, B3);
  Adder_part #(.width(1)) adder_1 (.a(A3), .b(not_1_out), .out(C3), .cin(adder_2_cout), .cout(Borrow));
  not not_2 (not_2_out, B2);
  Adder_part #(.width(1)) adder_2 (.a(A2), .b(not_2_out), .out(C2), .cin(adder_3_cout), .cout(adder_2_cout));
  not not_3 (not_3_out, B1);
  Adder_part #(.width(1)) adder_3 (.a(A1), .b(not_3_out), .out(C1), .cin(adder_4_cout), .cout(adder_3_cout));
  not not_4 (not_4_out, B0);
  Adder_part #(.width(1)) adder_4 (.a(A0), .b(not_4_out), .out(C0), .cin(1'b1), .cout(adder_4_cout));
endmodule
