// Logisim project BCD_adder.circ as structural Verilog: 1 circuit, main circuit main
module main (
  input  [3:0] in_1,
  input  [3:0] in_2,
  output out_3,
  output [3:0] out_4
);

  wire adder_1_cout, and_1_out, or_1_out;
  wire [3:0] adder_1_out;

  Adder #(.width(4)) adder_1 (.a(in_1), .b(in_2), .out(adder_1_out), .cout(adder_1_cout));  // open: cin
  or or_1 (or_1_out, adder_1_out[1], adder_1_out[2]);
  and and_1 (and_1_out, or_1_out, adder_1_out[3]);
  or or_2 (out_3, and_1_out, adder_1_cout);
  Adder #(.width(4)) adder_2 (.a({1'b0, {2{out_3}}, 1'b0}), .b(adder_1_out), .out(out_4));  // open: cin, cout

  // Notes on the sheet:
  //   BCD Adder
  //   Shrey Viradiya
endmodule
