// Logisim project BCD_counter.circ as structural Verilog: 1 circuit, main circuit main
module main (
  input  in_1,
  output out_2,
  output out_3,
  output out_4,
  output out_5
);

  wire and_1_out, clock_1_out, not_1_out, xor_1_out, xor_2_out, xor_3_out;

  Clock clock_1 (.out(clock_1_out));
  xor xor_1 (xor_1_out, xor_3_out, in_1);
  xor xor_2 (xor_2_out, in_1, out_4);
  xor xor_3 (xor_3_out, in_1, out_5);
  J_K_Flip_Flop j_k_ff_1 (.J(and_1_out), .clk(xor_1_out), .K(1'b1), .Q(out_2));  // open: Qn, preset, en, reset
  J_K_Flip_Flop j_k_ff_2 (.J(1'b1), .clk(xor_2_out), .K(1'b1), .Q(out_3));  // open: Qn, preset, en, reset
  J_K_Flip_Flop j_k_ff_3 (.J(not_1_out), .clk(xor_3_out), .K(1'b1), .Q(out_4));  // open: Qn, preset, en, reset
  J_K_Flip_Flop j_k_ff_4 (.J(1'b1), .clk(clock_1_out), .K(1'b1), .Q(out_5));  // open: Qn, preset, en, reset
  not not_1 (not_1_out, out_2);
  and and_1 (and_1_out, out_4, out_3);
endmodule
