// Logisim project Binary2Grey.circ as structural Verilog: 1 circuit, main circuit main
module main (
  input  A,
  input  A_2,
  input  B,
  input  B_2,
  input  C,
  input  C_2,
  input  D,
  input  D_2,
  input  x,
  input  y,
  input  z,
  output out_12,
  output out_13,
  output out_14,
  output out_15,
  output out_16,
  output out_17,
  output out_18,
  output out_19,
  output a_3,
  output b_3,
  output c_3,
  output d_3,
  output f,
  output e
);

  wire not_1_out, not_2_out, not_3_out, or_1_out, xor_4_out;

  not not_1 (not_1_out, z);
  xor xor_1 (out_14, A, B);
  xor xor_2 (out_16, B, C);
  not not_2 (not_2_out, y);
  xor xor_3 (out_18, C, D);
  or or_1 (or_1_out, not_2_out, z);
  and and_1 (b_3, x, or_1_out);
  xor xor_4 (xor_4_out, x, y);
  and and_2 (d_3, not_1_out, y);
  not not_3 (not_3_out, z);
  and and_3 (a_3, x, y);
  and and_4 (c_3, xor_4_out, z);
  and and_5 (e, z, not_3_out);
  xor xor_5 (out_15, A_2, B_2);
  xor xor_6 (out_17, out_15, C_2);
  xor xor_7 (out_19, out_17, D_2);

  assign f = z;
  assign out_12 = A;
  assign out_13 = A_2;

  // Notes on the sheet:
  //   Binary to Gray Code Conversion
  //   3-bit number square
  //   Gray to Binary Conversion
endmodule
