// Logisim project Counter.circ as structural Verilog: 1 circuit, main circuit main
module main (
  output out_1,
  output out_2,
  output out_3,
  output out_4,
  output out_5,
  output out_6,
  output out_7,
  output out_8,
  output out_9,
  output out_10,
  output out_11,
  output out_12
);

  wire and_1_out, button_1_out, clock_1_out, clock_2_out, not_4_out, not_5_out, not_6_out, not_7_out;

  Clock clock_1 (.out(clock_1_out));
  J_K_Flip_Flop j_k_ff_1 (.J(1'b1), .clk(clock_1_out), .K(1'b1), .Q(out_3));  // open: Qn, preset, en, reset
  J_K_Flip_Flop j_k_ff_2 (.J(1'b1), .clk(out_3), .K(1'b1), .Q(out_7));  // open: Qn, preset, en, reset
  J_K_Flip_Flop j_k_ff_3 (.J(1'b1), .clk(out_7), .K(1'b1), .Q(out_11));  // open: Qn, preset, en, reset
  not not_1 (out_4, out_3);
  not not_2 (out_8, out_7);
  not not_3 (out_12, out_11);
  Clock clock_2 (.out(clock_2_out));
  T_Flip_Flop t_ff_1 (.clk(clock_2_out), .T(1'b1), .Q(out_1));  // open: Qn, preset, reset, en
  not not_4 (not_4_out, out_1);
  T_Flip_Flop t_ff_2 (.clk(not_4_out), .T(1'b1), .Q(out_5));  // open: Qn, preset, reset, en
  not not_5 (not_5_out, out_5);
  T_Flip_Flop t_ff_3 (.clk(not_5_out), .T(1'b1), .Q(out_9));  // open: Qn, preset, reset, en
  Button button_1 (.out(button_1_out));
  J_K_Flip_Flop j_k_ff_4 (.J(1'b1), .clk(button_1_out), .K(1'b1), .Q(out_2));  // open: Qn, preset, en, reset
  J_K_Flip_Flop j_k_ff_5 (.J(1'b1), .clk(not_7_out), .K(1'b1), .Q(out_6), .reset(and_1_out));  // open: Qn, preset, en
  not not_6 (not_6_out, out_6);
  J_K_Flip_Flop j_k_ff_6 (.J(1'b1), .clk(not_6_out), .K(1'b1), .Q(out_10));  // open: Qn, preset, en, reset
  not not_7 (not_7_out, out_2);
  and and_1 (and_1_out, out_6, out_10);

  // Notes on the sheet:
  //   JK FlipFlop Counter
  //   T FlipFlop Counter
  //   JK FlipFlop Counter
endmodule
