// Logisim project Digital clock - Extended.circ as structural Verilog: 7 circuits, main circuit mod3
module _24_Hr_Digital_Clock (
);

  wire and_1_out, clock_1_out, display_1_a_2, display_1_b_2, display_1_c_2, display_1_d_2, display_1_e,
       display_1_f, display_1_g, display_2_a_2, display_2_b_2, display_2_c_2, display_2_d_2, display_2_e,
       display_2_f, display_2_g, display_3_a_2, display_3_b_2, display_3_c_2, display_3_d_2, display_3_e,
       display_3_f, display_3_g, display_4_a_2, display_4_b_2, display_4_c_2, display_4_d_2, display_4_e,
       display_4_f, display_4_g, display_5_a_2, display_5_b_2, display_5_c_2, display_5_d_2, display_5_e,
       display_5_f, display_5_g, display_6_a_2, display_6_b_2, display_6_c_2, display_6_d_2, display_6_e,
       display_6_f, display_6_g, mod3_1_c, mod3_1_d, mod6_1_b, mod6_1_c, mod6_1_d, mod6_2_b, mod6_2_c,
       mod6_2_d, mod9_1_a, mod9_1_b, mod9_1_c, mod9_1_d, mod9_2_a, mod9_2_b, mod9_2_c, mod9_2_d, mod9_3_a,
       mod9_3_b, mod9_3_c, mod9_3_d, nor_1_out, nor_2_out, nor_3_out, nor_4_out, nor_5_out, nor_6_out,
       nor_7_out, not_1_out, not_2_out, or_1_out, Reset_out, set_hour_out, SET_HRS_out, set_mins_2_out,
       SET_MINS_out, SET_SECS_out, settinguptime_1_a3, settinguptime_1_a4, settinguptime_1_a5,
       settinguptime_1_a6, settinguptime_1_b3, settinguptime_1_b4, settinguptime_1_b5, settinguptime_1_b6,
       settinguptime_1_c3, settinguptime_1_c4, settinguptime_1_c5, settinguptime_1_c6, settinguptime_1_d3,
       settinguptime_1_d4, settinguptime_1_d5, settinguptime_1_d6, settinguptime_1_e3, settinguptime_1_e4,
       settinguptime_1_e5, settinguptime_1_e6, settinguptime_1_f3, settinguptime_1_f4, settinguptime_1_f5,
       settinguptime_1_f6, settinguptime_1_g3, settinguptime_1_g4, settinguptime_1_g5, settinguptime_1_g6,
       timechecker_1_out_58, xor_1_out, xor_2_out;

  _7_Segment_Display u_7_segment_display_1 (
    .g(display_1_g), .f(display_1_f), .a(display_1_a_2), .b(display_1_b_2), .e(display_1_e),
    .d(display_1_d_2), .c(display_1_c_2));  // open: dp
  display display_1 (
    .A(1'b0), .B(1'b0), .C(mod3_1_c), .D(mod3_1_d), .a_2(display_1_a_2), .b_2(display_1_b_2),
    .c_2(display_1_c_2), .d_2(display_1_d_2), .e(display_1_e), .f(display_1_f), .g(display_1_g));
  not not_1 (not_1_out, mod3_1_c);
  nor nor_1 (nor_1_out, mod9_1_b, mod9_1_c, mod9_1_a, mod9_1_d);
  mod3 mod3_1 (.CLEAR(and_1_out), .CP(nor_1_out), .C(mod3_1_c), .D(mod3_1_d));
  and and_1 (and_1_out, nor_2_out, nor_3_out);
  nor nor_2 (nor_2_out, not_1_out, mod3_1_d, 1'b0, 1'b0);
  _7_Segment_Display u_7_segment_display_2 (
    .g(display_2_g), .f(display_2_f), .a(display_2_a_2), .b(display_2_b_2), .e(display_2_e),
    .d(display_2_d_2), .c(display_2_c_2));  // open: dp
  not not_2 (not_2_out, mod9_1_b);
  nor nor_3 (nor_3_out, not_2_out, mod9_1_d, mod9_1_a, mod9_1_c);
  display display_2 (
    .A(mod9_1_a), .B(mod9_1_b), .C(mod9_1_c), .D(mod9_1_d), .a_2(display_2_a_2), .b_2(display_2_b_2),
    .c_2(display_2_c_2), .d_2(display_2_d_2), .e(display_2_e), .f(display_2_f), .g(display_2_g));
  mod9 mod9_1 (.CLEAR(and_1_out), .CP(xor_1_out), .A(mod9_1_a), .B(mod9_1_b), .C(mod9_1_c), .D(mod9_1_d));
  xor xor_1 (xor_1_out, nor_4_out, SET_HRS_out);
  Button SET_HRS (.out(SET_HRS_out));
  _7_Segment_Display u_7_segment_display_3 (
    .g(display_3_g), .f(display_3_f), .a(display_3_a_2), .b(display_3_b_2), .e(display_3_e),
    .d(display_3_d_2), .c(display_3_c_2));  // open: dp
  nor nor_4 (nor_4_out, mod6_1_c, 1'b0, mod6_1_b, mod6_1_d);
  display display_3 (
    .A(1'b0), .B(mod6_1_b), .C(mod6_1_c), .D(mod6_1_d), .a_2(display_3_a_2), .b_2(display_3_b_2),
    .c_2(display_3_c_2), .d_2(display_3_d_2), .e(display_3_e), .f(display_3_f), .g(display_3_g));
  nor nor_5 (nor_5_out, mod9_2_b, mod9_2_c, mod9_2_a, mod9_2_d);
  mod6 mod6_1 (.CP(nor_5_out), .B(mod6_1_b), .C(mod6_1_c), .D(mod6_1_d));
  _7_Segment_Display u_7_segment_display_4 (
    .g(display_4_g), .f(display_4_f), .a(display_4_a_2), .b(display_4_b_2), .e(display_4_e),
    .d(display_4_d_2), .c(display_4_c_2));  // open: dp
  display display_4 (
    .A(mod9_2_a), .B(mod9_2_b), .C(mod9_2_c), .D(mod9_2_d), .a_2(display_4_a_2), .b_2(display_4_b_2),
    .c_2(display_4_c_2), .d_2(display_4_d_2), .e(display_4_e), .f(display_4_f), .g(display_4_g));
  mod9 mod9_2 (.CP(xor_2_out), .A(mod9_2_a), .B(mod9_2_b), .C(mod9_2_c), .D(mod9_2_d));  // open: CLEAR
  xor xor_2 (xor_2_out, nor_6_out, SET_MINS_out);
  Button SET_MINS (.out(SET_MINS_out));
  _7_Segment_Display u_7_segment_display_5 (
    .g(display_5_g), .f(display_5_f), .a(display_5_a_2), .b(display_5_b_2), .e(display_5_e),
    .d(display_5_d_2), .c(display_5_c_2));  // open: dp
  nor nor_6 (nor_6_out, mod6_2_c, mod6_2_b, mod6_2_d);
  display display_5 (
    .A(1'b0), .B(mod6_2_b), .C(mod6_2_c), .D(mod6_2_d), .a_2(display_5_a_2), .b_2(display_5_b_2),
    .c_2(display_5_c_2), .d_2(display_5_d_2), .e(display_5_e), .f(display_5_f), .g(display_5_g));
  mod6 mod6_2 (.CP(nor_7_out), .B(mod6_2_b), .C(mod6_2_c), .D(mod6_2_d));
  _7_Segment_Display u_7_segment_display_6 (
    .g(display_6_g), .f(display_6_f), .a(display_6_a_2), .b(display_6_b_2), .e(display_6_e),
    .d(display_6_d_2), .c(display_6_c_2));  // open: dp
  nor nor_7 (nor_7_out, mod9_3_b, mod9_3_c, mod9_3_a, mod9_3_d);
  display display_6 (
    .A(mod9_3_a), .B(mod9_3_b), .C(mod9_3_c), .D(mod9_3_d), .a_2(display_6_a_2), .b_2(display_6_b_2),
    .c_2(display_6_c_2), .d_2(display_6_d_2), .e(display_6_e), .f(display_6_f), .g(display_6_g));
  mod9 mod9_3 (.CP(or_1_out), .A(mod9_3_a), .B(mod9_3_b), .C(mod9_3_c), .D(mod9_3_d));  // open: CLEAR
  or or_1 (or_1_out, SET_SECS_out, clock_1_out);
  Button SET_SECS (.out(SET_SECS_out));
  Clock clock_1 (.out(clock_1_out));
  _7_Segment_Display u_7_segment_display_7 (
    .g(settinguptime_1_g6), .f(settinguptime_1_f6), .a(settinguptime_1_a6), .b(settinguptime_1_b6),
    .e(settinguptime_1_e6), .d(settinguptime_1_d6), .c(settinguptime_1_c6));  // open: dp
  TimeChecker timechecker_1 (
    .in_1(Reset_out), .out_58(timechecker_1_out_58), .a1(settinguptime_1_g6), .b1(display_1_g),
    .a2(settinguptime_1_f6), .b2(display_1_f), .a3(settinguptime_1_e6), .b3(display_1_e),
    .a4(settinguptime_1_d6), .b4(display_1_d_2), .a5(settinguptime_1_c6), .b5(display_1_c_2),
    .a6(settinguptime_1_b6), .b6(display_1_b_2), .a7(settinguptime_1_a6), .b7(display_1_a_2),
    .a8(display_2_g), .b8(settinguptime_1_g5), .a9(display_2_f), .b9(settinguptime_1_f5), .a10(display_2_e),
    .b10(settinguptime_1_e5), .a11(display_2_d_2), .b11(settinguptime_1_d5), .a12(display_2_c_2),
    .b12(settinguptime_1_c5), .a13(display_2_b_2), .b13(settinguptime_1_b5), .a14(display_2_a_2),
    .b14(settinguptime_1_a5), .a15(display_3_g), .b15(settinguptime_1_g4), .a16(display_3_f),
    .b16(settinguptime_1_f4), .a17(display_3_e), .b17(settinguptime_1_e4), .a18(display_3_d_2),
    .b18(settinguptime_1_d4), .a19(display_3_c_2), .b19(settinguptime_1_c4), .a20(display_3_b_2),
    .b20(settinguptime_1_b4), .a21(display_3_a_2), .b21(settinguptime_1_a4), .a22(display_4_g),
    .b22(settinguptime_1_g3), .a23(display_4_f), .b23(settinguptime_1_f3), .a24(display_4_e),
    .b24(settinguptime_1_e3), .a25(display_4_d_2), .b25(settinguptime_1_d3), .a26(display_4_c_2),
    .b26(settinguptime_1_c3), .a27(display_4_b_2), .b27(settinguptime_1_b3), .a28(display_4_a_2),
    .b28(settinguptime_1_a3));
  _7_Segment_Display u_7_segment_display_8 (
    .g(settinguptime_1_g5), .f(settinguptime_1_f5), .a(settinguptime_1_a5), .b(settinguptime_1_b5),
    .e(settinguptime_1_e5), .d(settinguptime_1_d5), .c(settinguptime_1_c5));  // open: dp
  _7_Segment_Display u_7_segment_display_9 (
    .g(settinguptime_1_g4), .f(settinguptime_1_f4), .a(settinguptime_1_a4), .b(settinguptime_1_b4),
    .e(settinguptime_1_e4), .d(settinguptime_1_d4), .c(settinguptime_1_c4));  // open: dp
  _7_Segment_Display u_7_segment_display_10 (
    .g(settinguptime_1_g3), .f(settinguptime_1_f3), .a(settinguptime_1_a3), .b(settinguptime_1_b3),
    .e(settinguptime_1_e3), .d(settinguptime_1_d3), .c(settinguptime_1_c3));  // open: dp
  Button set_hour (.out(set_hour_out));
  Button set_mins_2 (.out(set_mins_2_out));
  SettingUpTime settinguptime_1 (
    .d3(settinguptime_1_d3), .f6(settinguptime_1_f6), .f5(settinguptime_1_f5), .f4(settinguptime_1_f4),
    .f3(settinguptime_1_f3), .d6(settinguptime_1_d6), .d5(settinguptime_1_d5), .d4(settinguptime_1_d4),
    .e6(settinguptime_1_e6), .e5(settinguptime_1_e5), .e4(settinguptime_1_e4), .e3(settinguptime_1_e3),
    .c6(settinguptime_1_c6), .c5(settinguptime_1_c5), .c4(settinguptime_1_c4), .b6(settinguptime_1_b6),
    .b4(settinguptime_1_b4), .c3(settinguptime_1_c3), .a6(settinguptime_1_a6), .a4(settinguptime_1_a4),
    .b5(settinguptime_1_b5), .a5(settinguptime_1_a5), .b3(settinguptime_1_b3), .a3(settinguptime_1_a3),
    .Set_Minute(set_mins_2_out), .Set_Hour(set_hour_out), .g6(settinguptime_1_g6), .g5(settinguptime_1_g5),
    .g4(settinguptime_1_g4), .g3(settinguptime_1_g3));
  LED led_1 (.in(timechecker_1_out_58));
  Button Reset (.out(Reset_out));

  // Notes on the sheet:
  //   HOURS
  //   DE Project By
  //   Shrey Viradiya 18BCE259
  //   Tirth Patel 18BCE244
  //   Vansh Kamdar 18BCE254
  //   MINUTES
  //   24 HR DIGITAL CLOCK
  //   SECONDS
  //   Set Alarm
  //   Alarm Output
endmodule

module mod3 (
  input  CP,
  input  CLEAR,
  output C,
  output D
);

  wire and_1_out, d_ff_1_qn, d_ff_2_qn;

  and and_1 (and_1_out, d_ff_2_qn, d_ff_1_qn);
  D_Flip_Flop d_ff_1 (.clk(CP), .D(D), .Q(C), .Qn(d_ff_1_qn), .reset(CLEAR));  // open: preset, en
  D_Flip_Flop d_ff_2 (.clk(CP), .D(and_1_out), .Q(D), .Qn(d_ff_2_qn), .reset(CLEAR));  // open: preset, en
endmodule

module mod6 (
  input  CP,
  output B,
  output C,
  output D
);

  wire and_1_out, and_2_out, and_3_out, and_4_out, d_ff_1_qn, d_ff_2_qn, d_ff_3_qn, or_1_out, or_2_out;

  and and_1 (and_1_out, C, D);
  and and_2 (and_2_out, B, d_ff_3_qn);
  and and_3 (and_3_out, C, d_ff_3_qn);
  and and_4 (and_4_out, d_ff_1_qn, d_ff_2_qn, D);
  or or_1 (or_1_out, and_1_out, and_2_out);
  or or_2 (or_2_out, and_3_out, and_4_out);
  D_Flip_Flop d_ff_1 (.clk(CP), .D(or_1_out), .Q(B), .Qn(d_ff_1_qn));  // open: preset, en, reset
  D_Flip_Flop d_ff_2 (.clk(CP), .D(or_2_out), .Q(C), .Qn(d_ff_2_qn));  // open: preset, en, reset
  D_Flip_Flop d_ff_3 (.clk(CP), .D(d_ff_3_qn), .Q(D), .Qn(d_ff_3_qn));  // open: preset, en, reset
endmodule

module mod9 (
  input  CLEAR,
  input  CP,
  output A,
  output B,
  output C,
  output D
);

  wire and_1_out, and_2_out, and_3_out, and_4_out, and_5_out, d_ff_1_qn, d_ff_3_qn, d_ff_4_qn, or_1_out,
       or_2_out, xor_1_out;

  and and_1 (and_1_out, A, d_ff_4_qn);
  and and_2 (and_2_out, B, C, D);
  and and_3 (and_3_out, C, D);
  and and_4 (and_4_out, C, d_ff_4_qn);
  and and_5 (and_5_out, d_ff_1_qn, D, d_ff_3_qn);
  or or_1 (or_1_out, and_1_out, and_2_out);
  xor xor_1 (xor_1_out, B, and_3_out);
  or or_2 (or_2_out, and_4_out, and_5_out);
  D_Flip_Flop d_ff_1 (.clk(CP), .D(or_1_out), .Q(A), .Qn(d_ff_1_qn), .reset(CLEAR));  // open: preset, en
  D_Flip_Flop d_ff_2 (.clk(CP), .D(xor_1_out), .Q(B), .reset(CLEAR));  // open: Qn, preset, en
  D_Flip_Flop d_ff_3 (.clk(CP), .D(or_2_out), .Q(C), .Qn(d_ff_3_qn), .reset(CLEAR));  // open: preset, en
  D_Flip_Flop d_ff_4 (.clk(CP), .D(d_ff_4_qn), .Q(D), .Qn(d_ff_4_qn), .reset(CLEAR));  // open: preset, en
endmodule

module display (
  input  A,
  input  B,
  input  C,
  input  D,
  output a_2,
  output b_2,
  output c_2,
  output d_2,
  output e,
  output f,
  output g
);

  wire and_1_out, and_2_out, and_3_out, and_4_out, and_5_out, and_6_out, and_7_out, and_8_out, and_9_out,
       and_10_out, and_11_out, and_12_out, and_13_out, and_14_out, and_15_out, and_16_out, and_17_out,
       and_18_out, and_19_out, and_20_out, and_21_out, and_22_out, and_23_out, and_24_out, and_25_out,
       and_26_out, and_27_out, not_1_out, not_2_out, not_3_out, not_4_out;

  not not_1 (not_1_out, A);
  not not_2 (not_2_out, B);
  not not_3 (not_3_out, D);
  not not_4 (not_4_out, C);
  and and_1 (and_1_out, not_1_out, C);
  and and_2 (and_2_out, not_1_out, B, D);
  and and_3 (and_3_out, not_2_out, not_4_out, not_3_out);
  and and_4 (and_4_out, A, not_2_out, not_4_out);
  and and_5 (and_5_out, not_1_out, not_2_out);
  and and_6 (and_6_out, not_1_out, not_4_out, not_3_out);
  and and_7 (and_7_out, not_1_out, C, D);
  and and_8 (and_8_out, A, not_2_out, not_4_out);
  and and_9 (and_9_out, not_1_out, B);
  and and_10 (and_10_out, not_1_out, D);
  and and_11 (and_11_out, not_2_out, not_4_out, not_3_out);
  and and_12 (and_12_out, A, not_2_out, not_4_out);
  and and_13 (and_13_out, not_1_out, C, not_3_out);
  and and_14 (and_14_out, not_1_out, not_2_out, C);
  and and_15 (and_15_out, not_2_out, not_4_out, not_3_out);
  and and_16 (and_16_out, A, not_2_out, not_4_out);
  and and_17 (and_17_out, not_1_out, B, not_4_out, D);
  and and_18 (and_18_out, not_1_out, C, not_3_out);
  and and_19 (and_19_out, not_2_out, not_4_out, not_3_out);
  and and_20 (and_20_out, not_1_out, B, not_4_out);
  and and_21 (and_21_out, not_1_out, not_4_out, not_3_out);
  and and_22 (and_22_out, not_1_out, B, not_3_out);
  and and_23 (and_23_out, A, not_2_out, not_4_out);
  and and_24 (and_24_out, not_1_out, C, not_3_out);
  and and_25 (and_25_out, not_1_out, not_2_out, C);
  and and_26 (and_26_out, not_1_out, B, not_4_out);
  and and_27 (and_27_out, A, not_2_out, not_4_out);
  or or_1 (a_2, and_1_out, and_2_out, and_3_out, and_4_out);
  or or_2 (b_2, and_5_out, and_6_out, and_7_out, and_8_out);
  or or_3 (c_2, and_9_out, and_10_out, and_11_out, and_12_out);
  or or_4 (d_2, and_13_out, and_14_out, and_15_out, and_16_out, and_17_out);
  or or_5 (e, and_18_out, and_19_out);
  or or_6 (f, and_20_out, and_21_out, and_22_out, and_23_out);
  or or_7 (g, and_24_out, and_25_out, and_26_out, and_27_out);
endmodule

module SettingUpTime (
  input  Set_Minute,
  input  Set_Hour,
  output g6,
  output g5,
  output g4,
  output g3,
  output d3,
  output f6,
  output f5,
  output f4,
  output f3,
  output d6,
  output d5,
  output d4,
  output e6,
  output e5,
  output e4,
  output e3,
  output c6,
  output c5,
  output c4,
  output b6,
  output b4,
  output c3,
  output a6,
  output a4,
  output b5,
  output a5,
  output b3,
  output a3
);

  wire and_1_out, mod3_1_c, mod3_1_d, mod6_1_b, mod6_1_c, mod6_1_d, mod9_1_a, mod9_1_b, mod9_1_c, mod9_1_d,
       mod9_2_a, mod9_2_b, mod9_2_c, mod9_2_d, nor_1_out, nor_2_out, nor_3_out, nor_4_out, nor_5_out,
       not_1_out, not_2_out, xor_1_out;

  display display_1 (
    .A(1'b0), .B(1'b0), .C(mod3_1_c), .D(mod3_1_d), .a_2(a6), .b_2(b6), .c_2(c6), .d_2(d6), .e(e6), .f(f6),
    .g(g6));
  not not_1 (not_1_out, mod3_1_c);
  nor nor_1 (nor_1_out, mod9_1_b, mod9_1_c, mod9_1_a, mod9_1_d);
  mod3 mod3_1 (.CLEAR(and_1_out), .CP(nor_1_out), .C(mod3_1_c), .D(mod3_1_d));
  and and_1 (and_1_out, nor_2_out, nor_3_out);
  nor nor_2 (nor_2_out, not_1_out, mod3_1_d, 1'b0, 1'b0);
  nor nor_3 (nor_3_out, not_2_out, mod9_1_d, mod9_1_a, mod9_1_c);
  not not_2 (not_2_out, mod9_1_b);
  display display_2 (
    .A(mod9_1_a), .B(mod9_1_b), .C(mod9_1_c), .D(mod9_1_d), .a_2(a5), .b_2(b5), .c_2(c5), .d_2(d5), .e(e5),
    .f(f5), .g(g5));
  mod9 mod9_1 (.CLEAR(and_1_out), .CP(xor_1_out), .A(mod9_1_a), .B(mod9_1_b), .C(mod9_1_c), .D(mod9_1_d));
  xor xor_1 (xor_1_out, nor_4_out, Set_Hour);
  nor nor_4 (nor_4_out, mod6_1_c, 1'b0, mod6_1_b, mod6_1_d);
  display display_3 (
    .A(1'b0), .B(mod6_1_b), .C(mod6_1_c), .D(mod6_1_d), .a_2(a4), .b_2(b4), .c_2(c4), .d_2(d4), .e(e4),
    .f(f4), .g(g4));
  mod6 mod6_1 (.CP(nor_5_out), .B(mod6_1_b), .C(mod6_1_c), .D(mod6_1_d));
  nor nor_5 (nor_5_out, mod9_2_b, mod9_2_c, mod9_2_a, mod9_2_d);
  display display_4 (
    .A(mod9_2_a), .B(mod9_2_b), .C(mod9_2_c), .D(mod9_2_d), .a_2(a3), .b_2(b3), .c_2(c3), .d_2(d3), .e(e3),
    .f(f3), .g(g3));
  mod9 mod9_2 (.CP(Set_Minute), .A(mod9_2_a), .B(mod9_2_b), .C(mod9_2_c), .D(mod9_2_d));  // open: CLEAR

  // Notes on the sheet:
  //   HOURS
  //   MINUTES
endmodule

module TimeChecker (
  input  in_1,
  input  a1,
  input  a2,
  input  a3,
  input  a4,
  input  a5,
  input  a6,
  input  a7,
  input  a8,
  input  a9,
  input  a10,
  input  a11,
  input  a12,
  input  a13,
  input  a14,
  input  a15,
  input  a16,
  input  a17,
  input  a18,
  input  a19,
  input  a20,
  input  a21,
  input  a22,
  input  a23,
  input  a24,
  input  a25,
  input  a26,
  input  a27,
  input  a28,
  input  b1,
  input  b2,
  input  b3,
  input  b4,
  input  b5,
  input  b6,
  input  b7,
  input  b8,
  input  b9,
  input  b10,
  input  b11,
  input  b12,
  input  b13,
  input  b14,
  input  b15,
  input  b16,
  input  b17,
  input  b18,
  input  b19,
  input  b20,
  input  b21,
  input  b22,
  input  b23,
  input  b24,
  input  b25,
  input  b26,
  input  b27,
  input  b28,
  output out_58
);

  wire or_1_out, or_2_out, t_ff_1_q, xor_1_out, xor_2_out, xor_3_out, xor_4_out, xor_5_out, xor_6_out,
       xor_7_out, xor_8_out, xor_9_out, xor_10_out, xor_11_out, xor_12_out, xor_13_out, xor_14_out,
       xor_15_out, xor_16_out, xor_17_out, xor_18_out, xor_19_out, xor_20_out, xor_21_out, xor_22_out,
       xor_23_out, xor_24_out, xor_25_out, xor_26_out, xor_27_out, xor_28_out, xor_29_out;

  xor xor_1 (xor_1_out, a1, b1);
  xor xor_2 (xor_2_out, a2, b2);
  xor xor_3 (xor_3_out, a4, b4);
  xor xor_4 (xor_4_out, a3, b3);
  xor xor_5 (xor_5_out, a5, b5);
  xor xor_6 (xor_6_out, a6, b6);
  xor xor_7 (xor_7_out, a7, b7);
  xor xor_8 (xor_8_out, or_2_out, in_1);
  xor xor_9 (xor_9_out, a8, b8);
  xor xor_10 (xor_10_out, a9, b9);
  T_Flip_Flop t_ff_1 (.clk(xor_8_out), .T(1'b1), .Q(t_ff_1_q));  // open: Qn, preset, reset, en
  xor xor_11 (xor_11_out, a10, b10);
  xor xor_12 (xor_12_out, a11, b11);
  xor xor_13 (xor_13_out, a12, b12);
  xor xor_14 (xor_14_out, a13, b13);
  not not_1 (out_58, or_1_out);
  or or_1 (or_1_out, t_ff_1_q, or_2_out);
  or or_2 (or_2_out, xor_1_out, xor_2_out, xor_4_out, xor_3_out, xor_5_out, xor_6_out, xor_7_out, xor_9_out, xor_10_out, xor_11_out, xor_12_out, xor_13_out, xor_14_out, xor_16_out, xor_15_out, xor_17_out, xor_19_out, xor_18_out, xor_20_out, xor_21_out, xor_22_out, xor_24_out, xor_23_out, xor_25_out, xor_26_out, xor_27_out, xor_28_out, xor_29_out);
  xor xor_15 (xor_15_out, a15, b15);
  xor xor_16 (xor_16_out, a14, b14);
  xor xor_17 (xor_17_out, a16, b16);
  xor xor_18 (xor_18_out, a18, b18);
  xor xor_19 (xor_19_out, a17, b17);
  xor xor_20 (xor_20_out, a19, b19);
  xor xor_21 (xor_21_out, a20, b20);
  xor xor_22 (xor_22_out, a21, b21);
  xor xor_23 (xor_23_out, a23, b23);
  xor xor_24 (xor_24_out, a22, b22);
  xor xor_25 (xor_25_out, a24, b24);
  xor xor_26 (xor_26_out, a25, b25);
  xor xor_27 (xor_27_out, a26, b26);
  xor xor_28 (xor_28_out, a27, b27);
  xor xor_29 (xor_29_out, a28, b28);
endmodule
