// Logisim project Digital clock.circ as structural Verilog: 5 circuits, main circuit 24 Hr Digital Clock
module _24_Hr_Digital_Clock (
);

  wire and_1_out, clock_1_out, display_1_a_2, display_1_b_2, display_1_c_2, display_1_d_2, display_1_e,
       display_1_f, display_1_g, display_2_a_2, display_2_b_2, display_2_c_2, display_2_d_2, display_2_e,
       display_2_f, display_2_g, display_3_a_2, display_3_b_2, display_3_c_2, display_3_d_2, display_3_e,
       display_3_f, display_3_g, display_4_a_2, display_4_b_2, display_4_c_2, display_4_d_2, display_4_e,
       display_4_f, display_4_g, display_5_a_2, display_5_b_2, display_5_c_2, display_5_d_2, display_5_e,
       display_5_f, display_5_g, display_6_a_2, display_6_b_2, display_6_c_2, display_6_d_2, display_6_e,
       display_6_f, display_6_g, mod3_1_c, mod3_1_d, mod6_1_b, mod6_1_c, mod6_1_d, mod6_2_b, mod6_2_c,
       mod6_2_d, mod9_1_a, mod9_1_b, mod9_1_c, mod9_1_d, mod9_2_a, mod9_2_b, mod9_2_c, mod9_2_d, mod9_3_a,
       mod9_3_b, mod9_3_c, mod9_3_d, nor_1_out, nor_2_out, nor_3_out, nor_4_out, nor_5_out, nor_6_out,
       nor_7_out, not_1_out, not_2_out, or_1_out, SET_HRS_out, SET_MINS_out, SET_SECS_out, xor_1_out,
       xor_2_out;

  _7_Segment_Display u_7_segment_display_1 (
    .g(display_1_g), .f(display_1_f), .a(display_1_a_2), .b(display_1_b_2), .e(display_1_e),
    .d(display_1_d_2), .c(display_1_c_2));  // open: dp
  display display_1 (
    .A(1'b0), .B(1'b0), .C(mod3_1_c), .D(mod3_1_d), .a_2(display_1_a_2), .b_2(display_1_b_2),
    .c_2(display_1_c_2), .d_2(display_1_d_2), .e(display_1_e), .f(display_1_f), .g(display_1_g));
  not not_1 (not_1_out, mod3_1_c);
  nor nor_1 (nor_1_out, mod9_1_b, mod9_1_c, mod9_1_a, mod9_1_d);
  mod3 mod3_1 (.CLEAR(and_1_out), .CP(nor_1_out), .C(mod3_1_c), .D(mod3_1_d));
  and and_1 (and_1_out, nor_2_out, nor_3_out);
  nor nor_2 (nor_2_out, not_1_out, mod3_1_d, 1'b0, 1'b0);
  nor nor_3 (nor_3_out, not_2_out, mod9_1_d, mod9_1_a, mod9_1_c);
  _7_Segment_Display u_7_segment_display_2 (
    .g(display_2_g), .f(display_2_f), .a(display_2_a_2), .b(display_2_b_2), .e(display_2_e),
    .d(display_2_d_2), .c(display_2_c_2));  // open: dp
  not not_2 (not_2_out, mod9_1_b);
  display display_2 (
    .A(mod9_1_a), .B(mod9_1_b), .C(mod9_1_c), .D(mod9_1_d), .a_2(display_2_a_2), .b_2(display_2_b_2),
    .c_2(display_2_c_2), .d_2(display_2_d_2), .e(display_2_e), .f(display_2_f), .g(display_2_g));
  mod9 mod9_1 (.CLEAR(and_1_out), .CP(xor_1_out), .A(mod9_1_a), .B(mod9_1_b), .C(mod9_1_c), .D(mod9_1_d));
  xor xor_1 (xor_1_out, nor_4_out, SET_HRS_out);
  Button SET_HRS (.out(SET_HRS_out));
  _7_Segment_Display u_7_segment_display_3 (
    .g(display_3_g), .f(display_3_f), .a(display_3_a_2), .b(display_3_b_2), .e(display_3_e),
    .d(display_3_d_2), .c(display_3_c_2));  // open: dp
  nor nor_4 (nor_4_out, mod6_1_c, 1'b0, mod6_1_b, mod6_1_d);
  display display_3 (
    .A(1'b0), .B(mod6_1_b), .C(mod6_1_c), .D(mod6_1_d), .a_2(display_3_a_2), .b_2(display_3_b_2),
    .c_2(display_3_c_2), .d_2(display_3_d_2), .e(display_3_e), .f(display_3_f), .g(display_3_g));
  mod6 mod6_1 (.CP(nor_5_out), .B(mod6_1_b), .C(mod6_1_c), .D(mod6_1_d));
  _7_Segment_Display u_7_segment_display_4 (
    .g(display_4_g), .f(display_4_f), .a(display_4_a_2), .b(display_4_b_2), .e(display_4_e),
    .d(display_4_d_2), .c(display_4_c_2));  // open: dp
  nor nor_5 (nor_5_out, mod9_2_b, mod9_2_c, mod9_2_a, mod9_2_d);
  display display_4 (
    .A(mod9_2_a), .B(mod9_2_b), .C(mod9_2_c), .D(mod9_2_d), .a_2(display_4_a_2), .b_2(display_4_b_2),
    .c_2(display_4_c_2), .d_2(display_4_d_2), .e(display_4_e), .f(display_4_f), .g(display_4_g));
  mod9 mod9_2 (.CP(xor_2_out), .A(mod9_2_a), .B(mod9_2_b), .C(mod9_2_c), .D(mod9_2_d));  // open: CLEAR
  xor xor_2 (xor_2_out, nor_6_out, SET_MINS_out);
  Button SET_MINS (.out(SET_MINS_out));
  _7_Segment_Display u_7_segment_display_5 (
    .g(display_5_g), .f(display_5_f), .a(display_5_a_2), .b(display_5_b_2), .e(display_5_e),
    .d(display_5_d_2), .c(display_5_c_2));  // open: dp
  nor nor_6 (nor_6_out, mod6_2_c, mod6_2_b, mod6_2_d);
  display display_5 (
    .A(1'b0), .B(mod6_2_b), .C(mod6_2_c), .D(mod6_2_d), .a_2(display_5_a_2), .b_2(display_5_b_2),
    .c_2(display_5_c_2), .d_2(display_5_d_2), .e(display_5_e), .f(display_5_f), .g(display_5_g));
  mod6 mod6_2 (.CP(nor_7_out), .B(mod6_2_b), .C(mod6_2_c), .D(mod6_2_d));
  _7_Segment_Display u_7_segment_display_6 (
    .g(display_6_g), .f(display_6_f), .a(display_6_a_2), .b(display_6_b_2), .e(display_6_e),
    .d(display_6_d_2), .c(display_6_c_2));  // open: dp
  nor nor_7 (nor_7_out, mod9_3_b, mod9_3_c, mod9_3_a, mod9_3_d);
  display display_6 (
    .A(mod9_3_a), .B(mod9_3_b), .C(mod9_3_c), .D(mod9_3_d), .a_2(display_6_a_2), .b_2(display_6_b_2),
    .c_2(display_6_c_2), .d_2(display_6_d_2), .e(display_6_e), .f(display_6_f), .g(display_6_g));
  mod9 mod9_3 (.CP(or_1_out), .A(mod9_3_a), .B(mod9_3_b), .C(mod9_3_c), .D(mod9_3_d));  // open: CLEAR
  or or_1 (or_1_out, SET_SECS_out, clock_1_out);
  Button SET_SECS (.out(SET_SECS_out));
  Clock clock_1 (.out(clock_1_out));

  // Notes on the sheet:
  //   HOURS
  //   24 HR DIGITAL CLOCK
  //   MINUTES
  //   SECONDS
endmodule

module mod3 (
  input  CP,
  input  CLEAR,
  output C,
  output D
);

  wire and_1_out, d_ff_1_qn, d_ff_2_qn;

  and and_1 (and_1_out, d_ff_2_qn, d_ff_1_qn);
  D_Flip_Flop d_ff_1 (.clk(CP), .D(D), .Q(C), .Qn(d_ff_1_qn), .reset(CLEAR));  // open: preset, en
  D_Flip_Flop d_ff_2 (.clk(CP), .D(and_1_out), .Q(D), .Qn(d_ff_2_qn), .reset(CLEAR));  // open: preset, en
endmodule

module mod6 (
  input  CP,
  output B,
  output C,
  output D
);

  wire and_1_out, and_2_out, and_3_out, and_4_out, d_ff_1_qn, d_ff_2_qn, d_ff_3_qn, or_1_out, or_2_out;

  and and_1 (and_1_out, C, D);
  and and_2 (and_2_out, B, d_ff_3_qn);
  and and_3 (and_3_out, C, d_ff_3_qn);
  and and_4 (and_4_out, d_ff_1_qn, d_ff_2_qn, D);
  or or_1 (or_1_out, and_1_out, and_2_out);
  or or_2 (or_2_out, and_3_out, and_4_out);
  D_Flip_Flop d_ff_1 (.clk(CP), .D(or_1_out), .Q(B), .Qn(d_ff_1_qn));  // open: preset, en, reset
  D_Flip_Flop d_ff_2 (.clk(CP), .D(or_2_out), .Q(C), .Qn(d_ff_2_qn));  // open: preset, en, reset
  D_Flip_Flop d_ff_3 (.clk(CP), .D(d_ff_3_qn), .Q(D), .Qn(d_ff_3_qn));  // open: preset, en, reset
endmodule

module mod9 (
  input  CLEAR,
  input  CP,
  output A,
  output B,
  output C,
  output D
);

  wire and_1_out, and_2_out, and_3_out, and_4_out, and_5_out, d_ff_1_qn, d_ff_3_qn, d_ff_4_qn, or_1_out,
       or_2_out, xor_1_out;

  and and_1 (and_1_out, A, d_ff_4_qn);
  and and_2 (and_2_out, B, C, D);
  and and_3 (and_3_out, C, D);
  and and_4 (and_4_out, C, d_ff_4_qn);
  and and_5 (and_5_out, d_ff_1_qn, D, d_ff_3_qn);
  or or_1 (or_1_out, and_1_out, and_2_out);
  xor xor_1 (xor_1_out, B, and_3_out);
  or or_2 (or_2_out, and_4_out, and_5_out);
  D_Flip_Flop d_ff_1 (.clk(CP), .D(or_1_out), .Q(A), .Qn(d_ff_1_qn), .reset(CLEAR));  // open: preset, en
  D_Flip_Flop d_ff_2 (.clk(CP), .D(xor_1_out), .Q(B), .reset(CLEAR));  // open: Qn, preset, en
  D_Flip_Flop d_ff_3 (.clk(CP), .D(or_2_out), .Q(C), .Qn(d_ff_3_qn), .reset(CLEAR));  // open: preset, en
  D_Flip_Flop d_ff_4 (.clk(CP), .D(d_ff_4_qn), .Q(D), .Qn(d_ff_4_qn), .reset(CLEAR));  // open: preset, en
endmodule

module display (
  input  A,
  input  B,
  input  C,
  input  D,
  output a_2,
  output b_2,
  output c_2,
  output d_2,
  output e,
  output f,
  output g
);

  wire and_1_out, and_2_out, and_3_out, and_4_out, and_5_out, and_6_out, and_7_out, and_8_out, and_9_out,
       and_10_out, and_11_out, and_12_out, and_13_out, and_14_out, and_15_out, and_16_out, and_17_out,
       and_18_out, and_19_out, and_20_out, and_21_out, and_22_out, and_23_out, and_24_out, and_25_out,
       and_26_out, and_27_out, not_1_out, not_2_out, not_3_out, not_4_out;

  not not_1 (not_1_out, A);
  not not_2 (not_2_out, B);
  not not_3 (not_3_out, D);
  not not_4 (not_4_out, C);
  and and_1 (and_1_out, not_1_out, C);
  and and_2 (and_2_out, not_1_out, B, D);
  and and_3 (and_3_out, not_2_out, not_4_out, not_3_out);
  and and_4 (and_4_out, A, not_2_out, not_4_out);
  and and_5 (and_5_out, not_1_out, not_2_out);
  and and_6 (and_6_out, not_1_out, not_4_out, not_3_out);
  and and_7 (and_7_out, not_1_out, C, D);
  and and_8 (and_8_out, A, not_2_out, not_4_out);
  and and_9 (and_9_out, not_1_out, B);
  and and_10 (and_10_out, not_1_out, D);
  and and_11 (and_11_out, not_2_out, not_4_out, not_3_out);
  and and_12 (and_12_out, A, not_2_out, not_4_out);
  and and_13 (and_13_out, not_1_out, C, not_3_out);
  and and_14 (and_14_out, not_1_out, not_2_out, C);
  and and_15 (and_15_out, not_2_out, not_4_out, not_3_out);
  and and_16 (and_16_out, A, not_2_out, not_4_out);
  and and_17 (and_17_out, not_1_out, B, not_4_out, D);
  and and_18 (and_18_out, not_1_out, C, not_3_out);
  and and_19 (and_19_out, not_2_out, not_4_out, not_3_out);
  and and_20 (and_20_out, not_1_out, B, not_4_out);
  and and_21 (and_21_out, not_1_out, not_4_out, not_3_out);
  and and_22 (and_22_out, not_1_out, B, not_3_out);
  and and_23 (and_23_out, A, not_2_out, not_4_out);
  and and_24 (and_24_out, not_1_out, C, not_3_out);
  and and_25 (and_25_out, not_1_out, not_2_out, C);
  and and_26 (and_26_out, not_1_out, B, not_4_out);
  and and_27 (and_27_out, A, not_2_out, not_4_out);
  or or_1 (a_2, and_1_out, and_2_out, and_3_out, and_4_out);
  or or_2 (b_2, and_5_out, and_6_out, and_7_out, and_8_out);
  or or_3 (c_2, and_9_out, and_10_out, and_11_out, and_12_out);
  or or_4 (d_2, and_13_out, and_14_out, and_15_out, and_16_out, and_17_out);
  or or_5 (e, and_18_out, and_19_out);
  or or_6 (f, and_20_out, and_21_out, and_22_out, and_23_out);
  or or_7 (g, and_24_out, and_25_out, and_26_out, and_27_out);
endmodule
