// Logisim project Excess3Adder.circ as structural Verilog: 1 circuit, main circuit main
module main (
  input  [3:0] in_1,
  input  [3:0] in_2,
  output out_3,
  output [3:0] out_4
);

  wire adder_1_cout, and_1_out;
  wire [3:0] adder_1_out;

  Adder #(.width(4)) adder_1 (.a(in_1), .b(in_2), .out(adder_1_out), .cout(adder_1_cout));  // open: cin
  and and_1 (and_1_out, adder_1_out[0], adder_1_out[1]);
  or or_1 (out_3, and_1_out, adder_1_cout);
  Adder #(.width(4)) adder_2 (.a(4'b0011), .b(adder_1_out), .out(out_4));  // open: cin, cout

  // Notes on the sheet:
  //   Excess  3 Adder
  //   Answer
endmodule
