// Logisim project Exmaple.circ as structural Verilog: 1 circuit, main circuit main
module main (
  input  E,
  input  x,
  output out_3,
  output out_4
);

  wire button_1_out, xnor_1_out;

  xnor xnor_1 (xnor_1_out, x, out_4);
  Button button_1 (.out(button_1_out));
  J_K_Flip_Flop j_k_ff_1 (
    .J(xnor_1_out), .clk(button_1_out), .K(xnor_1_out), .Q(out_3));  // open: Qn, preset, en, reset
  J_K_Flip_Flop j_k_ff_2 (.J(E), .clk(button_1_out), .K(E), .Q(out_4));  // open: Qn, preset, en, reset
endmodule
