// Logisim project FlipFlop.circ as structural Verilog: 1 circuit, main circuit main
module main (
  input  R,
  input  S,
  input  CP,
  input  S_2,
  input  R_2,
  input  K,
  input  D,
  input  CP_2,
  input  J,
  input  K_2,
  input  T,
  input  CP_3,
  input  J_2,
  output Q,
  output Q_2,
  output Q_3,
  output Q_prime,
  output Q_prime_2,
  output Q_prime_3,
  output Q_prime_4,
  output Q_4,
  output Q_5,
  output Q_prime_5,
  output Q_6,
  output Q_7,
  output Q_prime_6,
  output Q_prime_7
);

  wire _1_out, _2_out, and_1_out, and_2_out, and_3_out, and_4_out, button_1_out, button_2_out, button_3_out,
       button_4_out, nand_3_out, nand_4_out, nand_5_out, nand_6_out, not_1_out;

  Button button_1 (.out(button_1_out));
  nor nor_1 (Q, R, Q_prime_2);
  nor nor_2 (Q_prime_2, Q, S_2);
  not not_1 (not_1_out, D);
  nand _1 (_1_out, D, CP_2);
  nand _2 (_2_out, CP_2, not_1_out);
  and and_1 (and_1_out, Q_7, T, button_1_out);
  and and_2 (and_2_out, button_1_out, T, Q_prime_7);
  Button button_2 (.out(button_2_out));
  Button button_3 (.out(button_3_out));
  nand _3 (Q_4, _1_out, Q_prime_5);
  nand _4 (Q_prime_5, Q_4, _2_out);
  nor nor_3 (Q_7, and_1_out, Q_prime_7);
  nor nor_4 (Q_prime_7, Q_7, and_2_out);
  nand nand_1 (Q_2, button_2_out, Q_prime);
  nand nand_2 (Q_prime, Q_2, button_3_out);
  Button button_4 (.out(button_4_out));
  nand nand_3 (nand_3_out, Q_5, K, button_4_out);
  nand nand_4 (nand_4_out, button_4_out, J, Q_prime_4);
  and and_3 (and_3_out, Q_6, K_2, CP_3);
  and and_4 (and_4_out, CP_3, J_2, Q_prime_6);
  nand nand_5 (nand_5_out, S, CP);
  nand nand_6 (nand_6_out, CP, R_2);
  nand nand_7 (Q_prime_4, nand_3_out, Q_5);
  nand nand_8 (Q_5, Q_prime_4, nand_4_out);
  nor nor_5 (Q_6, and_3_out, Q_prime_6);
  nor nor_6 (Q_prime_6, Q_6, and_4_out);
  nand nand_9 (Q_3, nand_5_out, Q_prime_3);
  nand nand_10 (Q_prime_3, Q_3, nand_6_out);

  // Notes on the sheet:
  //   CP
  //   RS Flip Flop
  //   D flipFlop
  //   T FlipFlop
  //   S
  //   R
  //   RS FlipFlop
  //   CP
  //   JK FlipFlop
  //   JK FlipFlop
  //   RS FlipFlop
endmodule
