// Logisim project HALF ADDER.circ as structural Verilog: 1 circuit, main circuit main
module main (
  input  [1:0] in_1,
  input  in_2,
  input  [1:0] in_3,
  output SUM,
  output CARRY,
  output SUM_2,
  output CARRY_2
);

  wire not_1_out;

  not not_1 (not_1_out, in_2);
  Multiplexer #(.select(2)) multiplexer_1 (
    .in0(1'b0), .in1(1'b1), .in2(1'b1), .in3(1'b0), .out(SUM), .sel(in_1));  // open: en
  Multiplexer #(.select(2)) multiplexer_2 (
    .in0(1'b0), .in1(1'b0), .in2(1'b0), .in3(1'b1), .out(CARRY), .sel(in_1));  // open: en
  Multiplexer #(.select(2)) multiplexer_3 (
    .in0(in_2), .in1(not_1_out), .in2(not_1_out), .in3(in_2), .out(SUM_2), .sel(in_3));  // open: en
  Multiplexer #(.select(2)) multiplexer_4 (
    .in0(1'b0), .in1(in_2), .in2(in_2), .in3(1'b1), .out(CARRY_2), .sel(in_3));  // open: en

  // Notes on the sheet:
  //   HALF ADDER
  //   FULL  ADDER
endmodule
