// Logisim project HALF SUB.circ as structural Verilog: 1 circuit, main circuit main
module main (
  input  [1:0] in_1,
  input  [1:0] in_2,
  output DIFFERENCE,
  output CARRY,
  output DIFFERENCE_2,
  output CARRY_2
);

  Multiplexer #(.select(2)) multiplexer_1 (
    .in0(1'b0), .in1(1'b1), .in2(1'b1), .in3(1'b0), .out(DIFFERENCE), .sel(in_1));  // open: en
  Multiplexer #(.select(2)) multiplexer_2 (
    .in0(1'b0), .in1(1'b1), .in2(1'b0), .in3(1'b0), .out(CARRY), .sel(in_1));  // open: en
  Multiplexer #(.select(2)) multiplexer_3 (.out(DIFFERENCE_2), .sel(in_2));  // open: in0, in1, in2, in3, en
  Multiplexer #(.select(2)) multiplexer_4 (.out(CARRY_2), .sel(in_2));  // open: in0, in1, in2, in3, en

  // Notes on the sheet:
  //   HALF SUBTRACTOR
  //   FULL SUBTRACTOR
endmodule
