// Logisim project LookAhead.circ as structural Verilog: 2 circuits, main circuit main
module main (
  input  A3,
  input  B3,
  input  A2,
  input  B2,
  input  A1,
  input  B1,
  input  A0,
  input  B0,
  input  C0,
  output out_10,
  output out_11,
  output out_12,
  output out_13,
  output out_14
);

  wire and_1_out, and_2_out, and_3_out, and_4_out, carryahead_1_c1, carryahead_1_c2, carryahead_1_c3,
       xor_1_out, xor_2_out, xor_3_out, xor_4_out;

  xor xor_1 (xor_1_out, A3, B3);
  and and_1 (and_1_out, A3, B3);
  xor xor_2 (xor_2_out, A2, B2);
  and and_2 (and_2_out, A2, B2);
  xor xor_3 (xor_3_out, A1, B1);
  and and_3 (and_3_out, A1, B1);
  xor xor_4 (xor_4_out, A0, B0);
  and and_4 (and_4_out, A0, B0);
  CarryAhead carryahead_1 (
    .p0(xor_4_out), .g0(and_4_out), .p1(xor_3_out), .g1(and_3_out), .p2(xor_2_out), .g2(and_2_out),
    .p3(xor_1_out), .g3(and_1_out), .c0(C0), .c1(carryahead_1_c1), .c2(carryahead_1_c2),
    .c3(carryahead_1_c3), .c4(out_10));
  xor xor_5 (out_11, xor_1_out, carryahead_1_c3);
  xor xor_6 (out_12, xor_2_out, carryahead_1_c2);
  xor xor_7 (out_13, carryahead_1_c1, xor_3_out);
  xor xor_8 (out_14, xor_4_out, C0);
endmodule

module CarryAhead (
  input  p0,
  input  g0,
  input  p1,
  input  g1,
  input  p2,
  input  g2,
  input  p3,
  input  g3,
  input  c0,
  output c1,
  output c2,
  output c3,
  output c4
);

  wire and_1_out, and_2_out, and_3_out, and_4_out, and_5_out, and_6_out, and_7_out, and_8_out, and_9_out,
       and_10_out;

  and and_1 (and_1_out, p0, c0);
  and and_2 (and_2_out, p1, g0);
  and and_3 (and_3_out, p1, p0, c0);
  and and_4 (and_4_out, p2, g1);
  and and_5 (and_5_out, p2, p1, g0);
  and and_6 (and_6_out, p2, p1, p0, c0);
  and and_7 (and_7_out, p3, g2);
  and and_8 (and_8_out, p3, p2, g1);
  and and_9 (and_9_out, p3, p2, p1, g0);
  and and_10 (and_10_out, p3, p2, p1, c0);
  or or_1 (c1, g0, and_1_out);
  or or_2 (c2, g1, and_2_out, and_3_out);
  or or_3 (c3, g2, and_4_out, and_5_out, and_6_out);
  or or_4 (c4, g3, and_7_out, and_8_out, and_9_out, and_10_out);
endmodule
