// Logisim project Multiplexer Implementation.circ as structural Verilog
module mux_simple (
  input  a,
  input  b,
  input  c,
  input  d,
  input  [3:0] in_5,
  input  [1:0] in_6,
  input  [1:0] in_7,
  output y,
  output out_9,
  output out_10
);

  wire and_1_out, and_2_out, and_3_out, multiplexer_2_out, multiplexer_3_out, multiplexer_4_out,
       multiplexer_5_out, not_1_out, not_2_out, not_3_out;

  not not_1 (not_1_out, a);
  not not_2 (not_2_out, c);
  and and_1 (and_1_out, not_1_out, not_2_out, d);
  and and_2 (and_2_out, b, c);
  and and_3 (and_3_out, a, b, not_3_out);
  not not_3 (not_3_out, d);
  or or_1 (y, and_1_out, and_2_out, and_3_out);
  Multiplexer #(.select(4)) multiplexer_1 (
    .in0(1'b0), .in1(1'b1), .in2(1'b0), .in3(1'b0), .in4(1'b0), .in5(1'b1), .in6(1'b1), .in7(1'b1),
    .in8(1'b0), .in9(1'b0), .in10(1'b0), .in11(1'b0), .in12(1'b1), .in13(1'b0), .in14(1'b1), .in15(1'b1),
    .out(out_10), .sel(in_5));  // open: en
  Multiplexer #(.select(2)) multiplexer_2 (
    .in0(1'b0), .in1(1'b1), .in2(1'b0), .in3(1'b0), .out(multiplexer_2_out), .sel(in_7));  // open: en
  Multiplexer #(.select(2)) multiplexer_3 (
    .in0(1'b0), .in1(1'b1), .in2(1'b1), .in3(1'b1), .out(multiplexer_3_out), .sel(in_7));  // open: en
  Multiplexer #(.select(2)) multiplexer_4 (
    .in0(1'b0), .in1(1'b0), .in2(1'b0), .in3(1'b0), .out(multiplexer_4_out), .sel(in_7));  // open: en
  Multiplexer #(.select(2)) multiplexer_5 (
    .in0(1'b1), .in1(1'b0), .in2(1'b1), .in3(1'b1), .out(multiplexer_5_out), .sel(in_7));  // open: en
  Multiplexer #(.select(2)) multiplexer_6 (
    .in0(multiplexer_2_out), .in1(multiplexer_3_out), .in2(multiplexer_4_out), .in3(multiplexer_5_out),
    .out(out_9), .sel(in_6));  // open: en

  // Notes on the sheet:
  //   Simple Circuit
  //   Using 16:1 Multiplexer
  //   Using 4:1 Multiplexer
endmodule
