// Logisim project Mutiplexer.circ as structural Verilog: 1 circuit, main circuit main
module main (
  input  [3:0] ABCD,
  output out_2,
  output out_3
);

  wire not_1_out;

  Multiplexer #(.select(4)) multiplexer_1 (
    .in0(1'b0), .in1(1'b1), .in2(1'b0), .in3(1'b0), .in4(1'b0), .in5(1'b1), .in6(1'b1), .in7(1'b1),
    .in8(1'b0), .in9(1'b0), .in10(1'b0), .in11(1'b0), .in12(1'b1), .in13(1'b0), .in14(1'b1), .in15(1'b1),
    .out(out_2), .sel(ABCD));  // open: en
  not not_1 (not_1_out, ABCD[0]);
  Multiplexer #(.select(3)) multiplexer_2 (
    .in0(ABCD[0]), .in1(1'b0), .in2(ABCD[0]), .in3(1'b1), .in4(1'b0), .in5(1'b0), .in6(not_1_out),
    .in7(1'b1), .out(out_3), .sel(ABCD[3:1]));  // open: en

  // Notes on the sheet:
  //   Multiplexer
endmodule
