// Logisim project SOME.circ as structural Verilog: 1 circuit, main circuit main
module main (
  input  [3:0] in_1,
  output out_2,
  output out_3,
  output out_4,
  output out_5
);

  wire decoder_1_out4, decoder_1_out5, decoder_1_out6, decoder_1_out7, decoder_1_out8, decoder_1_out9,
       decoder_1_out10, decoder_1_out11, decoder_1_out12;

  Decoder #(.select(4)) decoder_1 (
    .out4(decoder_1_out4), .out5(decoder_1_out5), .out6(decoder_1_out6), .out7(decoder_1_out7),
    .out8(decoder_1_out8), .out9(decoder_1_out9), .out10(decoder_1_out10), .out11(decoder_1_out11),
    .out12(decoder_1_out12), .sel(in_1));  // open: out0, out1, out2, out3, out13, out14, out15, en
  or or_1 (out_2, decoder_1_out7, decoder_1_out8, decoder_1_out9, decoder_1_out10);
  or or_2 (out_4, decoder_1_out9, decoder_1_out5, decoder_1_out6, decoder_1_out10);
  or or_3 (out_3, decoder_1_out11, decoder_1_out12);
  or or_4 (out_5, decoder_1_out12, decoder_1_out4, decoder_1_out6, decoder_1_out8, decoder_1_out10);
endmodule
