// Logisim project Serial2sCompliment.circ as structural Verilog: 1 circuit, main circuit main
module main (
);

  wire button_1_out, s_r_ff_1_q, shift_register_1_out, xor_1_out;

  Button button_1 (.out(button_1_out));
  Shift_Register shift_register_1 (
    .shift(1'b1), .in(xor_1_out), .clk(button_1_out), .out(shift_register_1_out));  // open: load, clr, d0, q0, d1, q1, d2, q2, d3, q3, d4, q4, d5, q5, d6, q6, d7, q7
  S_R_Flip_Flop s_r_ff_1 (
    .S(shift_register_1_out), .clk(button_1_out), .R(1'b0), .Q(s_r_ff_1_q));  // open: Qn, preset, reset, en
  xor xor_1 (xor_1_out, s_r_ff_1_q, shift_register_1_out);

  // Notes on the sheet:
  //   11000010 -> 00111110
endmodule
