// Logisim project SerialSub.circ as structural Verilog: 1 circuit, main circuit main
module main (
);

  wire and_1_out, and_2_out, clock_1_out, j_k_ff_1_q, not_1_out, shift_register_1_out, shift_register_2_out,
       xor_1_out;

  Clock clock_1 (.out(clock_1_out));
  Shift_Register #(.length(4)) shift_register_1 (
    .shift(1'b1), .in(xor_1_out), .clk(clock_1_out), .out(shift_register_1_out));  // open: load, clr, d0, q0, d1, q1, d2, q2, d3, q3
  Shift_Register #(.length(4)) shift_register_2 (
    .shift(1'b1), .in(1'b0), .clk(clock_1_out), .out(shift_register_2_out));  // open: load, clr, d0, q0, d1, q1, d2, q2, d3, q3
  not not_1 (not_1_out, shift_register_1_out);
  and and_1 (and_1_out, not_1_out, shift_register_2_out);
  and and_2 (and_2_out, clock_1_out, 1'b1);
  J_K_Flip_Flop j_k_ff_1 (
    .J(and_1_out), .clk(and_2_out), .K(shift_register_1_out), .Q(j_k_ff_1_q));  // open: Qn, preset, en, reset
  ExactlyOne xor_1 (.out(xor_1_out), .in1(shift_register_1_out), .in2(j_k_ff_1_q), .in3(shift_register_2_out));
endmodule
