// Logisim project SynchronousCounter.circ as structural Verilog: 4 circuits, main circuit main
module main (
  input  in_1,
  output out_2,
  output out_3,
  output out_4,
  output out_5,
  output out_6,
  output out_7,
  output out_8,
  output out_9,
  output out_10,
  output out_11,
  output out_12,
  output out_13,
  output out_14,
  output out_15,
  output out_16,
  output out_17,
  output out_18,
  output out_19,
  output out_20
);

  wire and_1_out, and_2_out, and_3_out, button_1_out, button_2_out, button_3_out, button_4_out, button_5_out,
       clock_1_out, clock_2_out, combinational_circuit_1_ja, combinational_circuit_1_jb,
       combinational_circuit_1_jc, combinational_circuit_1_jd, combinational_circuit_1_ka,
       combinational_circuit_1_kb, combinational_circuit_1_kc, combinational_circuit_1_kd,
       combinational_down_1_ja, combinational_down_1_jb, combinational_down_1_jc, combinational_down_1_jd,
       combinational_down_1_ka, combinational_down_1_kb, combinational_down_1_kc, combinational_down_1_kd,
       updown_1_ja, updown_1_jb, updown_1_jc, updown_1_jd, updown_1_ka, updown_1_kb, updown_1_kc,
       updown_1_kd, xor_1_out, xor_2_out;

  Button button_1 (.out(button_1_out));
  Clock clock_1 (.out(clock_1_out));
  Button button_2 (.out(button_2_out));
  xor xor_1 (xor_1_out, button_1_out, clock_1_out);
  Button button_3 (.out(button_3_out));
  J_K_Flip_Flop j_k_ff_1 (.J(1'b1), .clk(xor_1_out), .K(1'b1), .Q(out_5));  // open: Qn, preset, en, reset
  J_K_Flip_Flop j_k_ff_2 (.J(out_5), .clk(xor_1_out), .K(out_5), .Q(out_2));  // open: Qn, preset, en, reset
  J_K_Flip_Flop j_k_ff_3 (
    .J(combinational_circuit_1_ja), .clk(button_3_out), .K(combinational_circuit_1_ka), .Q(out_10));  // open: Qn, preset, en, reset
  J_K_Flip_Flop j_k_ff_4 (
    .J(combinational_down_1_ja), .clk(button_2_out), .K(combinational_down_1_ka), .Q(out_18));  // open: Qn, preset, en, reset
  and and_1 (and_1_out, out_5, out_2);
  J_K_Flip_Flop j_k_ff_5 (.J(and_1_out), .clk(xor_1_out), .K(and_1_out), .Q(out_3));  // open: Qn, preset, en, reset
  and and_2 (and_2_out, and_1_out, out_3);
  J_K_Flip_Flop j_k_ff_6 (.J(and_2_out), .clk(xor_1_out), .K(and_2_out), .Q(out_4));  // open: Qn, preset, en, reset
  Combinational_Circuit combinational_circuit_1 (
    .A(out_10), .B(out_9), .C(out_11), .D(out_12), .JA(combinational_circuit_1_ja),
    .KA(combinational_circuit_1_ka), .JB(combinational_circuit_1_jb), .KB(combinational_circuit_1_kb),
    .JC(combinational_circuit_1_jc), .KC(combinational_circuit_1_kc), .JD(combinational_circuit_1_jd),
    .KD(combinational_circuit_1_kd));
  J_K_Flip_Flop j_k_ff_7 (
    .J(combinational_circuit_1_jb), .clk(button_3_out), .K(combinational_circuit_1_kb), .Q(out_9));  // open: Qn, preset, en, reset
  Combinational_down combinational_down_1 (
    .A(out_18), .B(out_17), .C(out_19), .D(out_20), .ja(combinational_down_1_ja),
    .ka(combinational_down_1_ka), .jb(combinational_down_1_jb), .kb(combinational_down_1_kb),
    .jc(combinational_down_1_jc), .kc(combinational_down_1_kc), .jd(combinational_down_1_jd),
    .kd(combinational_down_1_kd));
  J_K_Flip_Flop j_k_ff_8 (
    .J(combinational_down_1_jb), .clk(button_2_out), .K(combinational_down_1_kb), .Q(out_17));  // open: Qn, preset, en, reset
  Button button_4 (.out(button_4_out));
  Clock clock_2 (.out(clock_2_out));
  and and_3 (and_3_out, out_7, out_8);
  xor xor_2 (xor_2_out, button_4_out, clock_2_out);
  J_K_Flip_Flop j_k_ff_9 (
    .J(combinational_circuit_1_jc), .clk(button_3_out), .K(combinational_circuit_1_kc), .Q(out_11));  // open: Qn, preset, en, reset
  J_K_Flip_Flop j_k_ff_10 (
    .J(combinational_down_1_jc), .clk(button_2_out), .K(combinational_down_1_kc), .Q(out_19));  // open: Qn, preset, en, reset
  J_K_Flip_Flop j_k_ff_11 (.J(and_3_out), .clk(xor_2_out), .K(and_3_out), .Q(out_6));  // open: Qn, preset, en, reset
  Button button_5 (.out(button_5_out));
  J_K_Flip_Flop j_k_ff_12 (
    .J(combinational_down_1_jd), .clk(button_2_out), .K(combinational_down_1_kd), .Q(out_20));  // open: Qn, preset, en, reset
  J_K_Flip_Flop j_k_ff_13 (.J(out_8), .clk(xor_2_out), .K(out_8), .Q(out_7));  // open: Qn, preset, en, reset
  J_K_Flip_Flop j_k_ff_14 (
    .J(combinational_circuit_1_jd), .clk(button_3_out), .K(combinational_circuit_1_kd), .Q(out_12));  // open: Qn, preset, en, reset
  J_K_Flip_Flop j_k_ff_15 (.J(1'b1), .clk(xor_2_out), .K(1'b1), .Q(out_8));  // open: Qn, preset, en, reset
  J_K_Flip_Flop j_k_ff_16 (
    .J(updown_1_ja), .clk(button_5_out), .K(updown_1_ka), .Q(out_14));  // open: Qn, preset, en, reset
  UpDown updown_1 (
    .kd(updown_1_kd), .jd(updown_1_jd), .kc(updown_1_kc), .jc(updown_1_jc), .kb(updown_1_kb),
    .jb(updown_1_jb), .ka(updown_1_ka), .ja(updown_1_ja), .A(out_14), .B(out_13), .C(out_15), .D(out_16),
    .ReverseInput(in_1));
  J_K_Flip_Flop j_k_ff_17 (
    .J(updown_1_jb), .clk(button_5_out), .K(updown_1_kb), .Q(out_13));  // open: Qn, preset, en, reset
  J_K_Flip_Flop j_k_ff_18 (
    .J(updown_1_jc), .clk(button_5_out), .K(updown_1_kc), .Q(out_15));  // open: Qn, preset, en, reset
  J_K_Flip_Flop j_k_ff_19 (
    .J(updown_1_jd), .clk(button_5_out), .K(updown_1_kd), .Q(out_16));  // open: Qn, preset, en, reset
endmodule

module Combinational_Circuit (
  input  A,
  input  B,
  input  C,
  input  D,
  output JA,
  output KA,
  output JB,
  output KB,
  output JC,
  output KC,
  output JD,
  output KD
);

  wire not_1_out;

  and and_1 (JA, B, C, D);
  and and_2 (JB, C, D);
  and and_3 (KB, C, D);
  not not_1 (not_1_out, A);
  and and_4 (JC, not_1_out, D);
  not not_2 (JD, D);

  assign KA = D;
  assign KC = D;
  assign KD = 1'b1;
endmodule

module Combinational_down (
  input  A,
  input  B,
  input  C,
  input  D,
  output ja,
  output ka,
  output jb,
  output kb,
  output jc,
  output kc,
  output jd,
  output kd
);

  wire and_4_out, and_5_out, not_1_out, not_2_out, not_3_out, not_5_out, not_6_out, not_7_out, not_8_out,
       not_9_out;

  not not_1 (not_1_out, B);
  not not_2 (not_2_out, C);
  and and_1 (ja, not_1_out, not_2_out, not_3_out);
  not not_3 (not_3_out, D);
  not not_4 (ka, D);
  and and_2 (jb, A, not_5_out);
  not not_5 (not_5_out, D);
  not not_6 (not_6_out, C);
  and and_3 (kb, not_6_out, not_7_out);
  not not_7 (not_7_out, D);
  and and_4 (and_4_out, B, not_8_out);
  not not_8 (not_8_out, D);
  and and_5 (and_5_out, A, not_9_out);
  not not_9 (not_9_out, D);
  not not_10 (kc, D);
  or or_1 (jc, and_4_out, and_5_out);

  assign jd = 1'b1;
  assign kd = 1'b1;
endmodule

module UpDown (
  input  ReverseInput,
  input  A,
  input  B,
  input  C,
  input  D,
  output kd,
  output jd,
  output kc,
  output jc,
  output kb,
  output jb,
  output ka,
  output ja
);

  wire [7:0] combinational_circuit_1_kd, combinational_down_1_kd;

  Combinational_Circuit combinational_circuit_1 (
    .A(A), .B(B), .C(C), .D(D), .JA(combinational_circuit_1_kd[7]), .KA(combinational_circuit_1_kd[6]),
    .JB(combinational_circuit_1_kd[5]), .KB(combinational_circuit_1_kd[4]),
    .JC(combinational_circuit_1_kd[3]), .KC(combinational_circuit_1_kd[2]),
    .JD(combinational_circuit_1_kd[1]), .KD(combinational_circuit_1_kd[0]));
  Combinational_down combinational_down_1 (
    .A(A), .B(B), .C(C), .D(D), .ja(combinational_down_1_kd[7]), .ka(combinational_down_1_kd[6]),
    .jb(combinational_down_1_kd[5]), .kb(combinational_down_1_kd[4]), .jc(combinational_down_1_kd[3]),
    .kc(combinational_down_1_kd[2]), .jd(combinational_down_1_kd[1]), .kd(combinational_down_1_kd[0]));
  Multiplexer #(.width(8)) multiplexer_1 (
    .in0(combinational_circuit_1_kd), .in1(combinational_down_1_kd), .out({ja, ka, jb, kb, jc, kc, jd, kd}),
    .sel(ReverseInput));  // open: en
endmodule
