// Logisim project VendorMachine.circ as structural Verilog: 1 circuit, main circuit main
module main (
  output out_1
);

  wire and_1_out, button_4_out, or_3_out;
  wire [4:0] or_2_out;
  wire [5:0] adder_1_out, register_1_q;

  Button button_1 (.out(or_2_out[4]));
  Button button_2 (.out(or_2_out[1]));
  Button button_3 (.out(or_2_out[2]));
  or or_1 (or_2_out[3], or_2_out[4], or_2_out[1]);
  or or_2 (or_2_out[0], or_2_out[2], or_2_out[4]);
  Adder #(.width(6)) adder_1 (.a({1'b0, or_2_out}), .b(register_1_q), .out(adder_1_out));  // open: cin, cout
  or or_3 (or_3_out, or_2_out[4], or_2_out[2], or_2_out[1]);
  Register #(.width(6), .trigger("falling")) register_1 (
    .D(adder_1_out), .Q(register_1_q), .clk(or_3_out), .clr(button_4_out));  // open: en
  Button button_4 (.out(button_4_out));
  or or_4 (out_1, register_1_q[5], and_1_out);
  and and_1 (and_1_out, register_1_q[1], register_1_q[2], register_1_q[3], register_1_q[4]);

  // Notes on the sheet:
  //   Q
  //   N
  //   D
endmodule
