// Logisim project bidirectional_shift.circ as structural Verilog: 1 circuit, main circuit main
module main (
  input  in_1,
  input  in_2,
  input  in_3,
  input  in_4,
  input  in_5,
  input  in_6,
  input  in_7,
  input  [1:0] in_8,
  input  in_9,
  input  in_10,
  input  in_11,
  input  in_12,
  input  in_13,
  input  in_14,
  output out_15,
  output out_16,
  output out_17,
  output out_18,
  output [2:0] out_19,
  output [2:0] out_20
);

  wire and_1_out, and_2_out, and_3_out, and_4_out, and_5_out, and_6_out, and_7_out, and_8_out, and_9_out,
       clock_1_out, clock_2_out, clock_3_out, clock_4_out, clock_5_out, clock_6_out, clock_7_out, d_ff_2_q,
       d_ff_4_q, d_ff_6_q, d_ff_8_q, d_ff_9_q, d_ff_10_q, d_ff_11_q, d_ff_12_q, j_k_ff_1_q, j_k_ff_2_q,
       j_k_ff_3_q, j_k_ff_4_q, j_k_ff_5_qn, j_k_ff_6_q, j_k_ff_7_qn, multiplexer_1_out, multiplexer_2_out,
       multiplexer_3_out, multiplexer_4_out, nand_1_out, nand_2_out, nand_3_out, nand_4_out, nand_5_out,
       nand_6_out, nand_7_out, nand_8_out, not_1_out, not_2_out, not_3_out, not_4_out, or_1_out, or_2_out,
       or_3_out;

  Clock clock_1 (.out(clock_1_out));
  Clock clock_2 (.out(clock_2_out));
  nand nand_1 (nand_1_out, nand_8_out, in_13, clock_2_out);
  nand nand_2 (nand_2_out, clock_2_out, in_14, nand_7_out);
  Clock clock_3 (.out(clock_3_out));
  Clock clock_4 (.out(clock_4_out));
  D_Flip_Flop d_ff_1 (.clk(clock_1_out), .D(multiplexer_1_out), .Q(out_15));  // open: Qn, preset, en, reset
  Multiplexer #(.select(2), .enable("false")) multiplexer_1 (
    .in0(out_15), .in1(out_17), .in2(out_16), .in3(in_9), .out(multiplexer_1_out), .sel(in_8));
  not not_1 (not_1_out, in_1);
  and and_1 (and_1_out, d_ff_2_q, in_1);
  or or_1 (or_1_out, and_1_out, and_3_out);
  D_Flip_Flop d_ff_2 (.clk(clock_3_out), .D(in_2), .Q(d_ff_2_q));  // open: Qn, preset, en, reset
  and and_2 (and_2_out, j_k_ff_2_q, j_k_ff_3_q);
  J_K_Flip_Flop j_k_ff_1 (
    .J(and_2_out), .clk(clock_4_out), .K(and_2_out), .Q(j_k_ff_1_q));  // open: Qn, preset, en, reset
  LED led_1 (.in(j_k_ff_1_q));
  not not_2 (not_2_out, clock_2_out);
  and and_3 (and_3_out, not_1_out, in_3);
  J_K_Flip_Flop j_k_ff_2 (
    .J(j_k_ff_3_q), .clk(clock_4_out), .K(j_k_ff_3_q), .Q(j_k_ff_2_q));  // open: Qn, preset, en, reset
  D_Flip_Flop d_ff_3 (.clk(clock_1_out), .D(multiplexer_2_out), .Q(out_16), .reset(in_7));  // open: Qn, preset, en
  Multiplexer #(.select(2), .enable("false")) multiplexer_2 (
    .in0(out_16), .in1(out_15), .in2(out_18), .in3(in_10), .out(multiplexer_2_out), .sel(in_8));
  nand nand_3 (nand_3_out, nand_1_out, nand_4_out);
  nand nand_4 (nand_4_out, nand_3_out, nand_2_out);
  and and_4 (and_4_out, d_ff_4_q, in_1);
  and and_5 (and_5_out, not_1_out, in_4);
  or or_2 (or_2_out, and_4_out, and_5_out);
  D_Flip_Flop d_ff_4 (.clk(clock_3_out), .D(or_1_out), .Q(d_ff_4_q));  // open: Qn, preset, en, reset
  LED led_2 (.in(j_k_ff_2_q));
  D_Flip_Flop d_ff_5 (.clk(clock_1_out), .D(multiplexer_3_out), .Q(out_18), .reset(in_7));  // open: Qn, preset, en
  Multiplexer #(.select(2), .enable("false")) multiplexer_3 (
    .in0(out_18), .in1(out_16), .in2(out_17), .in3(in_11), .out(multiplexer_3_out), .sel(in_8));
  D_Flip_Flop d_ff_6 (.clk(clock_3_out), .D(or_2_out), .Q(d_ff_6_q));  // open: Qn, preset, en, reset
  J_K_Flip_Flop j_k_ff_3 (.J(1'b1), .clk(clock_4_out), .K(1'b1), .Q(j_k_ff_3_q));  // open: Qn, preset, en, reset
  LED led_3 (.in(j_k_ff_3_q));
  Multiplexer #(.select(2), .enable("false")) multiplexer_4 (
    .in0(out_17), .in1(out_18), .in2(out_15), .in3(in_12), .out(multiplexer_4_out), .sel(in_8));
  and and_6 (and_6_out, d_ff_6_q, in_1);
  and and_7 (and_7_out, not_1_out, in_5);
  or or_3 (or_3_out, and_6_out, and_7_out);
  D_Flip_Flop d_ff_7 (.clk(clock_1_out), .D(multiplexer_4_out), .Q(out_17), .reset(in_7));  // open: Qn, preset, en
  nand nand_5 (nand_5_out, nand_3_out, not_2_out);
  nand nand_6 (nand_6_out, not_2_out, nand_4_out);
  LED led_4 (.in(d_ff_8_q));
  D_Flip_Flop d_ff_8 (.clk(clock_3_out), .D(or_3_out), .Q(d_ff_8_q));  // open: Qn, preset, en, reset
  Clock clock_5 (.out(clock_5_out));
  Clock clock_6 (.out(clock_6_out));
  Clock clock_7 (.out(clock_7_out));
  nand nand_7 (nand_7_out, nand_5_out, nand_8_out);
  nand nand_8 (nand_8_out, nand_7_out, nand_6_out);
  D_Flip_Flop d_ff_9 (.clk(clock_5_out), .D(in_6), .Q(d_ff_9_q));  // open: Qn, preset, en, reset
  LED led_5 (.in(d_ff_9_q));
  J_K_Flip_Flop j_k_ff_4 (
    .J(1'b1), .clk(clock_6_out), .K(1'b1), .Q(j_k_ff_4_q), .Qn(out_19[0]), .preset(and_8_out));  // open: en, reset
  J_K_Flip_Flop j_k_ff_5 (
    .J(1'b1), .clk(clock_7_out), .K(1'b1), .Q(out_20[0]), .Qn(j_k_ff_5_qn), .reset(and_9_out));  // open: preset, en
  LED led_6 (.in(nand_7_out));
  LED led_7 (.in(nand_8_out));
  D_Flip_Flop d_ff_10 (.clk(clock_5_out), .D(d_ff_9_q), .Q(d_ff_10_q));  // open: Qn, preset, en, reset
  LED led_8 (.in(d_ff_10_q));
  J_K_Flip_Flop j_k_ff_6 (
    .J(1'b1), .clk(j_k_ff_4_q), .K(1'b1), .Q(j_k_ff_6_q), .Qn(out_19[1]), .preset(and_8_out));  // open: en, reset
  J_K_Flip_Flop j_k_ff_7 (
    .J(1'b1), .clk(j_k_ff_5_qn), .K(1'b1), .Q(out_20[1]), .Qn(j_k_ff_7_qn), .reset(and_9_out));  // open: preset, en
  D_Flip_Flop d_ff_11 (.clk(clock_5_out), .D(d_ff_10_q), .Q(d_ff_11_q));  // open: Qn, preset, en, reset
  J_K_Flip_Flop j_k_ff_8 (
    .J(1'b1), .clk(j_k_ff_6_q), .K(1'b1), .Qn(out_19[2]), .preset(and_8_out));  // open: Q, en, reset
  J_K_Flip_Flop j_k_ff_9 (
    .J(1'b1), .clk(j_k_ff_7_qn), .K(1'b1), .Q(out_20[2]), .reset(and_9_out));  // open: Qn, preset, en
  LED led_9 (.in(d_ff_11_q));
  D_Flip_Flop d_ff_12 (.clk(clock_5_out), .D(d_ff_11_q), .Q(d_ff_12_q));  // open: Qn, preset, en, reset
  LED led_10 (.in(d_ff_12_q));
  not not_3 (not_3_out, out_19[0]);
  not not_4 (not_4_out, out_20[0]);
  and and_8 (and_8_out, out_19[2], out_19[1], not_3_out);
  and and_9 (and_9_out, not_4_out, out_20[1], out_20[2]);
endmodule
