// Logisim project excess3add2.circ as structural Verilog: 1 circuit, main circuit main
module main (
  input  [3:0] in_1,
  input  [3:0] in_2,
  output [3:0] out_3,
  output [3:0] out_4,
  output out_5
);

  wire adder_1_cout, and_1_out, and_2_out, or_1_out;
  wire [3:3] not_1_out;

  Adder #(.width(4)) adder_1 (.a(in_1), .b(in_2), .out(out_3), .cout(adder_1_cout));  // open: cin
  or or_1 (or_1_out, out_3[0], out_3[1]);
  buf and_1 (and_1_out, out_3[2]);  // AND_Gate
  and and_2 (and_2_out, or_1_out, and_1_out);
  or or_2 (out_5, and_2_out, adder_1_cout);
  not not_1 (not_1_out[3], out_5);
  Adder #(.width(4)) adder_2 (.a(out_3), .b({{2{not_1_out[3]}}, out_5, 1'b1}), .out(out_4));  // open: cin, cout
endmodule
