// Logisim project modNCounter.circ as structural Verilog: 1 circuit, main circuit main
module main (
  input  [3:0] in_1,
  output [3:0] out_2
);

  wire button_1_out, comparator_1_eq, t_ff_1_qn, t_ff_2_qn, t_ff_3_qn;

  Button button_1 (.out(button_1_out));
  T_Flip_Flop t_ff_1 (
    .clk(button_1_out), .T(1'b1), .Q(out_2[0]), .Qn(t_ff_1_qn), .reset(comparator_1_eq));  // open: preset, en
  T_Flip_Flop t_ff_2 (
    .clk(t_ff_1_qn), .T(1'b1), .Q(out_2[1]), .Qn(t_ff_2_qn), .reset(comparator_1_eq));  // open: preset, en
  T_Flip_Flop t_ff_3 (
    .clk(t_ff_2_qn), .T(1'b1), .Q(out_2[2]), .Qn(t_ff_3_qn), .reset(comparator_1_eq));  // open: preset, en
  T_Flip_Flop t_ff_4 (.clk(t_ff_3_qn), .T(1'b1), .Q(out_2[3]), .reset(comparator_1_eq));  // open: Qn, preset, en
  Comparator #(.width(4)) comparator_1 (.a(out_2), .b(in_1), .eq(comparator_1_eq));  // open: gt, lt
endmodule
