// Logisim project prac6.circ as structural Verilog: 1 circuit, main circuit main
module main (
  input  [2:0] A__B__C,
  input  D,
  output out_3
);

  wire not_1_out;

  not not_1 (not_1_out, D);
  Multiplexer #(.select(3)) multiplexer_1 (
    .in0(D), .in1(1'b0), .in2(D), .in3(1'b1), .in4(1'b0), .in5(1'b0), .in6(not_1_out), .in7(1'b1),
    .out(out_3), .sel(A__B__C));  // open: en

  // Notes on the sheet:
  //   8 X 1 MULTIPLEXER
endmodule
