// Logisim project priority encoder.circ as structural Verilog: 2 circuits, main circuit main
module main (
  input  [7:0] in_1,
  output [2:0] out_2
);

  anything anything_1 (
    .d0(in_1[0]), .d1(in_1[1]), .d2(in_1[2]), .d3(in_1[3]), .d4(in_1[4]), .d5(in_1[5]), .d6(in_1[6]),
    .d7(in_1[7]), .a(out_2[2]), .b(out_2[1]), .c(out_2[0]));
endmodule

module anything (
  input  d0,
  input  d1,
  input  d2,
  input  d3,
  input  d4,
  input  d5,
  input  d6,
  input  d7,
  output a,
  output b,
  output c
);

  wire and_1_out, and_2_out, and_3_out, and_4_out, and_5_out, and_6_out, and_7_out, and_8_out, and_9_out,
       and_10_out, and_11_out, and_12_out, not_1_out, not_2_out, not_3_out, not_4_out, not_5_out, not_6_out,
       not_7_out, not_8_out, not_9_out, not_10_out, not_11_out, not_12_out, not_13_out, not_14_out,
       not_15_out, not_16_out, not_17_out, not_18_out, not_19_out, not_20_out, not_21_out, not_22_out,
       not_23_out, not_24_out, not_25_out, not_26_out, not_27_out, not_28_out, not_29_out, not_30_out,
       not_31_out, not_32_out, not_33_out, not_34_out, not_35_out, not_36_out, not_37_out, not_38_out;

  not not_1 (not_1_out, d0);
  not not_2 (not_2_out, d1);
  not not_3 (not_3_out, d2);
  not not_4 (not_4_out, d3);
  not not_5 (not_5_out, d0);
  not not_6 (not_6_out, d1);
  not not_7 (not_7_out, d2);
  not not_8 (not_8_out, d3);
  not not_9 (not_9_out, d0);
  not not_10 (not_10_out, d1);
  not not_11 (not_11_out, d2);
  not not_12 (not_12_out, d3);
  not not_13 (not_13_out, d0);
  not not_14 (not_14_out, d1);
  not not_15 (not_15_out, d2);
  not not_16 (not_16_out, d3);
  not not_17 (not_17_out, d0);
  not not_18 (not_18_out, d1);
  not not_19 (not_19_out, d4);
  not not_20 (not_20_out, d5);
  not not_21 (not_21_out, d0);
  not not_22 (not_22_out, d1);
  not not_23 (not_23_out, d4);
  not not_24 (not_24_out, d5);
  not not_25 (not_25_out, d0);
  not not_26 (not_26_out, d1);
  not not_27 (not_27_out, d0);
  not not_28 (not_28_out, d1);
  not not_29 (not_29_out, d0);
  not not_30 (not_30_out, d2);
  not not_31 (not_31_out, d4);
  not not_32 (not_32_out, d6);
  not not_33 (not_33_out, d0);
  not not_34 (not_34_out, d2);
  not not_35 (not_35_out, d4);
  not not_36 (not_36_out, d0);
  not not_37 (not_37_out, d2);
  not not_38 (not_38_out, d0);
  and and_1 (and_1_out, not_1_out, not_2_out, not_3_out, not_4_out, d7);
  and and_2 (and_2_out, not_5_out, not_6_out, not_7_out, not_8_out, d6);
  and and_3 (and_3_out, not_9_out, not_10_out, not_11_out, not_12_out, d5);
  and and_4 (and_4_out, not_13_out, not_14_out, not_15_out, not_16_out, d4);
  and and_5 (and_5_out, not_17_out, not_18_out, not_19_out, not_20_out, d7);
  and and_6 (and_6_out, not_21_out, not_22_out, not_23_out, not_24_out, d6);
  and and_7 (and_7_out, not_25_out, not_26_out, d3);
  and and_8 (and_8_out, not_27_out, not_28_out, d2);
  and and_9 (and_9_out, not_29_out, not_30_out, not_31_out, not_32_out, d7);
  and and_10 (and_10_out, not_33_out, not_34_out, not_35_out, d5);
  and and_11 (and_11_out, not_36_out, not_37_out, d3);
  and and_12 (and_12_out, not_38_out, d1);
  or or_1 (a, and_1_out, and_2_out, and_3_out, and_4_out);
  or or_2 (b, and_5_out, and_6_out, and_7_out, and_8_out);
  or or_3 (c, and_9_out, and_10_out, and_11_out, and_12_out);
endmodule
