// Logisim project probleem 1.circ as structural Verilog
module problem_1 (
  input  a,
  input  b,
  input  c,
  input  d,
  output y
);

  wire nand_1_out, nand_2_out, nand_3_out, nand_4_out;

  nand nand_1 (nand_1_out, a, b);
  nand nand_2 (nand_2_out, b, c);
  nand nand_3 (nand_3_out, c, d);
  nand nand_4 (nand_4_out, a, d);
  nand nand_5 (y, nand_1_out, nand_2_out, nand_3_out, nand_4_out);
endmodule

module problem_2 (
  input  a,
  input  b,
  input  c,
  input  d,
  output y
);

  wire nand_1_out, nand_2_out, nand_3_out, nand_4_out, nand_5_out, nand_6_out, nand_7_out;

  nand nand_1 (nand_1_out, d, d);
  nand nand_2 (nand_2_out, a, a);
  nand nand_3 (nand_3_out, a, a);
  nand nand_4 (nand_4_out, d, d);
  nand nand_5 (nand_5_out, c, nand_1_out);
  nand nand_6 (nand_6_out, nand_2_out, c);
  nand nand_7 (nand_7_out, nand_3_out, nand_4_out);
  nand nand_8 (y, nand_5_out, nand_6_out, nand_7_out);
endmodule

module problem_2_simple (
  input  a,
  input  b,
  input  c,
  input  d,
  output y
);

  wire and_1_out, and_2_out, and_3_out, not_1_out, not_2_out, not_3_out, not_4_out;

  and and_1 (and_1_out, c, not_1_out);
  not not_1 (not_1_out, d);
  not not_2 (not_2_out, a);
  and and_2 (and_2_out, not_2_out, c);
  not not_3 (not_3_out, a);
  and and_3 (and_3_out, not_3_out, not_4_out);
  not not_4 (not_4_out, d);
  or or_1 (y, and_1_out, and_2_out, and_3_out);
endmodule
