// Logisim project serialSubtractor.circ as structural Verilog: 1 circuit, main circuit main
module main (
);

  wire adder_1_cout, adder_1_out, button_1_out, d_ff_1_q, not_1_out, shift_register_1_out,
       shift_register_2_out;

  Button button_1 (.out(button_1_out));
  Shift_Register #(.length(4)) shift_register_1 (
    .shift(1'b1), .in(adder_1_out), .clk(button_1_out), .out(shift_register_1_out));  // open: load, clr, d0, q0, d1, q1, d2, q2, d3, q3
  Shift_Register #(.length(4)) shift_register_2 (
    .shift(1'b1), .clk(button_1_out), .out(shift_register_2_out));  // open: in, load, clr, d0, q0, d1, q1, d2, q2, d3, q3
  not not_1 (not_1_out, shift_register_2_out);
  Adder #(.width(1)) adder_1 (
    .a(shift_register_1_out), .b(not_1_out), .out(adder_1_out), .cin(d_ff_1_q), .cout(adder_1_cout));
  D_Flip_Flop d_ff_1 (.clk(button_1_out), .D(adder_1_cout), .Q(d_ff_1_q));  // open: Qn, preset, en, reset
endmodule
