// Logisim project shift register.circ as structural Verilog: 1 circuit, main circuit main
module main (
  input  [1:0] in_1,
  input  [3:0] in_2
);

  wire button_1_out, clock_1_out, d_ff_1_q, d_ff_2_q, d_ff_3_q, d_ff_4_q, multiplexer_1_out,
       multiplexer_2_out, multiplexer_3_out, multiplexer_4_out;

  Clock clock_1 (.out(clock_1_out));
  Multiplexer #(.select(2)) multiplexer_1 (
    .in0(d_ff_1_q), .in1(d_ff_4_q), .in2(d_ff_2_q), .in3(in_2[3]), .out(multiplexer_1_out), .sel(in_1));  // open: en
  Multiplexer #(.select(2)) multiplexer_2 (
    .in0(d_ff_2_q), .in1(d_ff_1_q), .in2(d_ff_3_q), .in3(in_2[2]), .out(multiplexer_2_out), .sel(in_1));  // open: en
  Multiplexer #(.select(2)) multiplexer_3 (
    .in0(d_ff_3_q), .in1(d_ff_2_q), .in2(d_ff_4_q), .in3(in_2[1]), .out(multiplexer_3_out), .sel(in_1));  // open: en
  Multiplexer #(.select(2)) multiplexer_4 (
    .in0(d_ff_4_q), .in1(d_ff_3_q), .in2(d_ff_1_q), .in3(in_2[0]), .out(multiplexer_4_out), .sel(in_1));  // open: en
  D_Flip_Flop d_ff_1 (
    .clk(clock_1_out), .D(multiplexer_1_out), .Q(d_ff_1_q), .reset(button_1_out));  // open: Qn, preset, en
  D_Flip_Flop d_ff_2 (
    .clk(clock_1_out), .D(multiplexer_2_out), .Q(d_ff_2_q), .reset(button_1_out));  // open: Qn, preset, en
  D_Flip_Flop d_ff_3 (
    .clk(clock_1_out), .D(multiplexer_3_out), .Q(d_ff_3_q), .reset(button_1_out));  // open: Qn, preset, en
  D_Flip_Flop d_ff_4 (
    .clk(clock_1_out), .D(multiplexer_4_out), .Q(d_ff_4_q), .reset(button_1_out));  // open: Qn, preset, en
  Button button_1 (.out(button_1_out));
  LED led_1 (.in(d_ff_1_q));
  LED led_2 (.in(d_ff_2_q));
  LED led_3 (.in(d_ff_3_q));
  LED led_4 (.in(d_ff_4_q));

  // Notes on the sheet:
  //   Shift Register
  //   00 - No Change
  //   01 - Right Shift 
  //   10- Left Shift
  //   11- Parallel Load
endmodule
